// Logisim project decodificador.circ as structural Verilog: 1 circuit, main circuit decodificador
module decodificador (
  input  [31:0] instrucao,
  output [6:0] opcode,
  output [4:0] rd,
  output [2:0] funct3,
  output [4:0] rs1,
  output [4:0] rs2,
  output [6:0] funct7,
  output [31:0] imm
);

  wire Auipc, Btype, Jal, Jalr, Lui, Stype;
  wire [2:0] or_2_out;
  wire [31:0] extensorsinal_12_1_saida, extensorsinal_12_2_saida, extensorsinal_13_1_saida,
       extensorsinal_21_1_saida, extensorzero_20_typeu_1_saida;

  and S (Stype, instrucao[0], instrucao[1], ~instrucao[2], ~instrucao[3], ~instrucao[4], instrucao[5], ~instrucao[6]);  // AND_Gate
  and B (Btype, instrucao[0], instrucao[1], ~instrucao[2], ~instrucao[3], ~instrucao[4], instrucao[5], instrucao[6]);  // AND_Gate
  and u_Jal (Jal, instrucao[0], instrucao[1], instrucao[2], instrucao[3], ~instrucao[4], instrucao[5], instrucao[6]);  // AND_Gate
  and u_Jalr (Jalr, instrucao[0], instrucao[1], instrucao[2], ~instrucao[3], ~instrucao[4], instrucao[5], instrucao[6]);  // AND_Gate
  and u_Lui (Lui, instrucao[0], instrucao[1], instrucao[2], ~instrucao[3], instrucao[4], instrucao[5], ~instrucao[6]);  // AND_Gate
  and u_Auipc (Auipc, instrucao[0], instrucao[1], instrucao[2], ~instrucao[3], instrucao[4], ~instrucao[5], ~instrucao[6]);  // AND_Gate
  or or_1 (or_2_out[1], Btype, Jal);
  or or_2 (or_2_out[0], Jal, Stype);
  or or_3 (or_2_out[2], Lui, Auipc);
  extensorSinal_12 extensorsinal_12_1 (.entrada(instrucao[31:20]), .saida(extensorsinal_12_1_saida));
  extensorSinal_12 extensorsinal_12_2 (.entrada({instrucao[31:25], instrucao[11:7]}), .saida(extensorsinal_12_2_saida));
  extensorSinal_13 extensorsinal_13_1 (
    .entrada({instrucao[31], instrucao[7], instrucao[30:25], instrucao[10:9], instrucao[11], instrucao[8], 1'b0}),
    .saida(extensorsinal_13_1_saida));
  extensorSinal_21 extensorsinal_21_1 (
    .entrada({instrucao[31], instrucao[19:12], instrucao[20], instrucao[30:21], 1'b0}),
    .saida(extensorsinal_21_1_saida));
  extensorZero_20_typeU extensorzero_20_typeu_1 (.entrada(instrucao[31:12]), .saida(extensorzero_20_typeu_1_saida));
  Multiplexer #(.select(3), .width(32)) multiplexer_1 (
    .in0(extensorsinal_12_1_saida), .in1(extensorsinal_12_2_saida), .in2(extensorsinal_13_1_saida),
    .in3(extensorsinal_21_1_saida), .in4(extensorzero_20_typeu_1_saida), .out(imm), .sel(or_2_out));  // open: in5, in6, in7
  // Probe on imm

  assign funct3 = instrucao[14:12];
  assign funct7 = instrucao[31:25];
  assign opcode = instrucao[6:0];
  assign rd = instrucao[11:7];
  assign rs1 = instrucao[19:15];
  assign rs2 = instrucao[24:20];

  // Other names for the same wires on the sheet: Btype_imm[12:1] = {instrucao[31], instrucao[7], instrucao[30:25], instrucao[10:9], instrucao[11], instrucao[8]};
  //   imm_5[4:0] = instrucao[11:7]; Stype_imm[11:0] = {instrucao[31:25], instrucao[11:7]};
  //   imm_12[11:0] = instrucao[31:20]; imm_20[19:0] = instrucao[31:12]; Itype_imm[11:0] = instrucao[31:20];
  //   Jtype_imm[20:1] = {instrucao[31], instrucao[19:12], instrucao[20], instrucao[30:21]};
  //   Utype_imm[19:0] = instrucao[31:12]; imm_7[6:0] = instrucao[31:25]

  // Notes on the sheet:
  //   0100011
  //   1100011
  //   1101111
  //   1100111
  //   0110111
  //   1100111
  //   Tipo I
  //   Tipo S
  //   Tipo B
  //   Tipo U
  //   Tipo J
  //   immSrc
endmodule
