// Logisim project extensoresSinal.circ as structural Verilog: 9 circuits, main circuit extensorSinal_1
module extensorSinal_1 (
  input  entrada,
  output [31:0] saida
);

  // Probe on entrada
  // Probe on {{31{1'b0}}, entrada}

  assign saida = {{31{1'b0}}, entrada};
endmodule

module extensorSinal_8 (
  input  [7:0] entrada,
  output [31:0] saida
);

  // Probe on entrada
  // Probe on {{25{entrada[7]}}, entrada[6:0]}

  assign saida = {{25{entrada[7]}}, entrada[6:0]};
endmodule

module extensorZero_8 (
  input  [7:0] entrada,
  output [31:0] saida
);

  // Probe on entrada
  // Probe on {{24{1'b0}}, entrada}

  assign saida = {{24{1'b0}}, entrada};
endmodule

module extensorSinal_12 (
  input  [11:0] entrada,
  output [31:0] saida
);

  // Probe on entrada
  // Probe on {{21{entrada[11]}}, entrada[10:0]}

  assign saida = {{21{entrada[11]}}, entrada[10:0]};
endmodule

module extensorSinal_13 (
  input  [12:0] entrada,
  output [31:0] saida
);

  // Probe on entrada
  // Probe on {{20{entrada[12]}}, entrada[11:0]}

  assign saida = {{20{entrada[12]}}, entrada[11:0]};
endmodule

module extensorSinal_16 (
  input  [15:0] entrada,
  output [31:0] saida
);

  // Probe on entrada
  // Probe on {{17{entrada[15]}}, entrada[14:0]}

  assign saida = {{17{entrada[15]}}, entrada[14:0]};
endmodule

module extensorZero_16 (
  input  [15:0] entrada,
  output [31:0] saida
);

  // Probe on entrada
  // Probe on {{16{1'b0}}, entrada}

  assign saida = {{16{1'b0}}, entrada};
endmodule

module extensorZero_20_typeU (
  input  [19:0] entrada,
  output [31:0] saida
);

  // Probe on entrada
  // Probe on {entrada, {12{1'b0}}}

  assign saida = {entrada, {12{1'b0}}};
endmodule

module extensorSinal_21 (
  input  [20:0] entrada,
  output [31:0] saida
);

  // Probe on entrada
  // Probe on {{12{entrada[20]}}, entrada[19:0]}

  assign saida = {{12{entrada[20]}}, entrada[19:0]};
endmodule
