// Logisim project memInstr.circ as structural Verilog: 1 circuit, main circuit memInstr
module memInstr (
  input  [31:0] PC_address,
  output [31:0] Instruction
);

  ROM #(.addrWidth(24), .dataWidth(32)) rom_1 (.addr(PC_address[25:2]), .data(Instruction));
endmodule
