// Logisim project idULA.circ as structural Verilog: 1 circuit, main circuit idULA
module idULA (
  input  [31:0] A,
  input  [31:0] B,
  input  [2:0] funct3,
  output Zero
);

  wire comparator_1_eq, comparator_1_lt, comparator_2_lt, not_1_out, not_2_out;

  Comparator #(.width(32)) comparator_1 (.a(A), .b(B), .eq(comparator_1_eq), .lt(comparator_1_lt));  // open: gt
  Comparator #(.mode("unsigned"), .width(32)) comparator_2 (.a(A), .b(B), .lt(comparator_2_lt));  // open: gt, eq
  not not_1 (not_1_out, comparator_1_lt);
  not not_2 (not_2_out, comparator_2_lt);
  Multiplexer #(.select(2)) multiplexer_1 (
    .in0(comparator_1_eq), .in2(not_1_out), .in3(not_2_out), .out(Zero), .sel(funct3[2:1]));  // open: in1

  // Notes on the sheet:
  //   EQ
  //   !LT
  //   !LTU
endmodule
