// Logisim project contadorCiclos.circ as structural Verilog: 1 circuit, main circuit contadorCiclos
module contadorCiclos (
  input  Clock,
  output [31:0] Contador
);

  wire [31:0] adder_1_out;

  Adder #(.width(32)) adder_1 (.a(Contador), .b(32'h1), .out(adder_1_out));  // open: cin, cout
  Register #(.width(32)) register_1 (.D(adder_1_out), .en(Clock), .clk(Clock), .Q(Contador));  // open: clr
endmodule
