// Logisim project main.circ as structural Verilog: 1 circuit, main circuit main
module main (
);

  wire ALUSrcB, and_1_out, and_2_out, and_3_out, Auipc, Branch, BranchSrc, CLK, Jalr, Jump, Lui, MemRead,
       MemToReg, MemWrite, PCSrc, RegWrite, Stop, sUnsigned, ucula_1_p5, ucula_1_p6, ucula_1_p7, Zero;
  wire [1:0] ALUOp, offset, ucenderecamento_1_size;
  wire [2:0] decodificador_1_funct3, funct3;
  wire [3:0] ucenderecamento_1_byteenable;
  wire [4:0] decodificador_1_rd, decodificador_1_rs1, decodificador_1_rs2;
  wire [6:0] decodificador_1_funct7, opcode;
  wire [31:0] adder_1_out, ALU, bancoregistradores_1_ld2, contadorciclos_1_contador, Imm, LD1, LD2,
       memdados_1_dados_lidos, meminstr_1_instruction, multiplexer_1_out, multiplexer_2_out,
       multiplexer_3_out, multiplexer_4_out, multiplexer_6_out, PC, PC_p4, WD;

  Adder #(.width(32)) adder_1 (.a(PC), .b(Imm), .out(adder_1_out));  // open: cin, cout
  Multiplexer #(.width(32)) multiplexer_1 (.in0(PC_p4), .in1(adder_1_out), .out(multiplexer_1_out), .sel(PCSrc));
  // Probe on Imm
  and and_1 (and_1_out, CLK, ~Stop);  // AND_Gate
  // Probe on contadorciclos_1_contador
  contadorCiclos contadorciclos_1 (.Clock(and_1_out), .Contador(contadorciclos_1_contador));
  Clock clock_1 (.out(CLK));
  Register #(.width(32)) u_PC (.D(multiplexer_2_out), .clk(and_2_out), .Q(PC));  // open: en, clr
  Multiplexer #(.width(32)) multiplexer_2 (.in0(multiplexer_1_out), .in1(ALU), .out(multiplexer_2_out), .sel(Jalr));
  and and_2 (and_2_out, CLK, ~Stop);  // AND_Gate
  // Probe on PC
  // Probe on LD1
  // Probe on LD2
  // Probe on ALU
  Adder #(.width(32)) adder_2 (.a(32'h4), .b(PC), .out(PC_p4));  // open: cin, cout
  memInstr meminstr_1 (.PC_address(PC), .Instruction(meminstr_1_instruction));
  // Probe on meminstr_1_instruction
  decodificador decodificador_1 (
    .instrucao(meminstr_1_instruction), .imm(Imm), .opcode(opcode), .rd(decodificador_1_rd),
    .funct3(decodificador_1_funct3), .rs1(decodificador_1_rs1), .rs2(decodificador_1_rs2),
    .funct7(decodificador_1_funct7));
  // Probe on opcode
  // Probe on decodificador_1_rs1
  // Probe on decodificador_1_rs2
  ucDesvio ucdesvio_1 (.Zero(Zero), .funct3(decodificador_1_funct3), .BranchSrc(BranchSrc));
  ucPrincipal ucprincipal_1 (
    .BranchSrc(BranchSrc), .opcode(opcode), .MemRead(MemRead), .MemWrite(MemWrite), .Jump(Jump),
    .Branch(Branch), .S_Jalr(Jalr), .RegWrite(RegWrite), .ALUOp(ALUOp), .Auipc_uc(Auipc), .ALUSrcB(ALUSrcB),
    .Lui_uc(Lui), .Stop(Stop), .MemToReg(MemToReg), .PCSrc(PCSrc));
  // Probe on decodificador_1_rd
  Multiplexer #(.width(32)) multiplexer_3 (.in0(WD), .in1(PC_p4), .out(multiplexer_3_out), .sel(Jump));
  bancoRegistradores bancoregistradores_1 (
    .RegWrite(RegWrite), .LR1(decodificador_1_rs1), .LR2(decodificador_1_rs2), .WD(multiplexer_3_out),
    .WR(decodificador_1_rd), .clk(CLK), .LD2(bancoregistradores_1_ld2), .LD1(LD1));
  // ucULA ucula_1: pin names not known; wires that end beside it: decodificador_1_funct3, decodificador_1_funct7, opcode, ALUOp, ucula_1_p5, ucula_1_p6, ucula_1_p7
  Multiplexer #(.width(32)) multiplexer_4 (.in0(LD1), .in1(PC), .out(multiplexer_4_out), .sel(Auipc));
  Multiplexer #(.width(32)) multiplexer_5 (.in0(bancoregistradores_1_ld2), .in1(Imm), .out(LD2), .sel(ALUSrcB));
  Multiplexer #(.width(32)) multiplexer_6 (
    .in0(multiplexer_4_out), .in1({32{1'b0}}), .out(multiplexer_6_out), .sel(Lui));
  // ULA ula_1: pin names not known; wires that end beside it: multiplexer_6_out, LD2, ucula_1_p5, ucula_1_p7, ucula_1_p6, Zero, ALU
  ucEnderecamento ucenderecamento_1 (
    .Adress(ALU), .Funct3(funct3), .writeEnable(MemWrite), .byteEnable(ucenderecamento_1_byteenable),
    .Size(ucenderecamento_1_size), .Offset(offset), .signal_unsigned(sUnsigned));
  memDados memdados_1 (
    .Endereco(ALU), .clk(and_3_out), .MemRead(MemRead), .byteEnable(ucenderecamento_1_byteenable),
    .dado(bancoregistradores_1_ld2), .size(ucenderecamento_1_size), .offset(offset), .sUnsigned(sUnsigned),
    .Dados_lidos(memdados_1_dados_lidos));
  and and_3 (and_3_out, CLK, ~Stop);  // AND_Gate
  Multiplexer #(.width(32)) multiplexer_7 (.in0(ALU), .in1(memdados_1_dados_lidos), .out(WD), .sel(MemToReg));

  // Notes on the sheet:
  //   rs1
  //   rs2
  //   rd
  //   rs2
  //   Imm
endmodule
