// Logisim project ImmGen.circ as structural Verilog: 1 circuit, main circuit immGen
module immGen (
  input  [31:0] instrucao,
  input  [2:0] ImmSrc,
  output [31:0] imm
);

  wire [31:0] extensorsinal_12_1_p2, extensorsinal_12_2_p2, extensorsinal_13_1_p2, extensorsinal_21_1_p2,
       extensorzero_20_typeu_1_p2;

  // extensorSinal_12 extensorsinal_12_1: pin names not known; wires that end beside it: instrucao[31:20], extensorsinal_12_1_p2
  // extensorSinal_12 extensorsinal_12_2: pin names not known; wires that end beside it: {instrucao[31:25], instrucao[11:7]}, extensorsinal_12_2_p2
  // extensorSinal_13 extensorsinal_13_1: pin names not known; wires that end beside it: {instrucao[31], instrucao[7], instrucao[30:25], instrucao[11:8], 1'b0}, extensorsinal_13_1_p2
  // extensorSinal_21 extensorsinal_21_1: pin names not known; wires that end beside it: {instrucao[31], instrucao[19:12], instrucao[20], instrucao[30:21], 1'b0}, extensorsinal_21_1_p2
  // extensorZero_20_typeU extensorzero_20_typeu_1: pin names not known; wires that end beside it: instrucao[31:12], extensorzero_20_typeu_1_p2
  // Probe on imm
  Multiplexer #(.select(3), .width(32)) multiplexer_1 (
    .in0(extensorsinal_12_1_p2), .in1(extensorsinal_12_2_p2), .in2(extensorsinal_13_1_p2),
    .in3(extensorsinal_21_1_p2), .in4(extensorzero_20_typeu_1_p2), .out(imm), .sel(ImmSrc));  // open: in5, in6, in7

  // Other names for the same wires on the sheet: Btype_imm[12:1] = {instrucao[31], instrucao[7], instrucao[30:25], instrucao[11:8]};
  //   imm_5[4:0] = instrucao[11:7]; Stype_imm[11:0] = {instrucao[31:25], instrucao[11:7]};
  //   imm_12[11:0] = instrucao[31:20]; imm_20[19:0] = instrucao[31:12]; Itype_imm[11:0] = instrucao[31:20];
  //   Jtype_imm[20:1] = {instrucao[31], instrucao[19:12], instrucao[20], instrucao[30:21]};
  //   Utype_imm[19:0] = instrucao[31:12]; imm_7[6:0] = instrucao[31:25]

  // Notes on the sheet:
  //   Tipo I
  //   Tipo S
  //   Tipo B
  //   Tipo U
  //   Tipo J
endmodule
