// Logisim project ULA.circ as structural Verilog: 1 circuit, main circuit ULA
module ULA (
  input  [31:0] A,
  input  [31:0] B,
  input  Branch,
  input  [2:0] ALUC,
  input  [6:0] funct7,
  input  [6:0] opcode,
  output sZero,
  output [31:0] Result
);

  wire and_1_out, comparator_1_lt, comparator_2_lt, or_1_out;
  wire [31:0] adder_1_out, and_2_out, extensorsinal_1_1_saida, extensorsinal_1_2_saida, multiplexer_1_out,
       multiplexer_2_out, or_2_out, shifter_1_out, shifter_2_out, shifter_3_out, subtractor_1_out, xor_1_out;

  and and_1 (and_1_out, funct7[5], opcode[5]);
  Adder #(.width(32)) adder_1 (.a(A), .b(B), .out(adder_1_out));  // open: cin, cout
  Subtractor #(.width(32)) subtractor_1 (.a(A), .b(B), .out(subtractor_1_out));  // open: bin, bout
  Shifter #(.shift("lr"), .width(32)) shifter_1 (.in(A), .\dist (B[4:0]), .out(shifter_1_out));
  Shifter #(.shift("ar"), .width(32)) shifter_2 (.in(A), .\dist (B[4:0]), .out(shifter_2_out));
  or or_1 (or_1_out, and_1_out, Branch);
  Multiplexer #(.width(32)) multiplexer_1 (
    .in0(adder_1_out), .in1(subtractor_1_out), .out(multiplexer_1_out), .sel(or_1_out));
  Shifter #(.width(32)) shifter_3 (.in(A), .\dist (B[4:0]), .out(shifter_3_out));
  Comparator #(.width(32)) comparator_1 (.a(A), .b(B), .lt(comparator_1_lt));  // open: gt, eq
  Comparator #(.mode("unsigned"), .width(32)) comparator_2 (.a(A), .b(B), .lt(comparator_2_lt));  // open: gt, eq
  assign xor_1_out = A ^ B;  // XOR_Gate xor_1, 32 bits wide
  Multiplexer #(.width(32)) multiplexer_2 (
    .in0(shifter_1_out), .in1(shifter_2_out), .out(multiplexer_2_out), .sel(funct7[5]));
  assign or_2_out = A | B;  // OR_Gate or_2, 32 bits wide
  assign and_2_out = A & B;  // AND_Gate and_2, 32 bits wide
  extensorSinal_1 extensorsinal_1_1 (.entrada(comparator_1_lt), .saida(extensorsinal_1_1_saida));
  extensorSinal_1 extensorsinal_1_2 (.entrada(comparator_2_lt), .saida(extensorsinal_1_2_saida));
  Multiplexer #(.select(3), .width(32)) multiplexer_3 (
    .in0(multiplexer_1_out), .in1(shifter_3_out), .in2(extensorsinal_1_1_saida),
    .in3(extensorsinal_1_2_saida), .in4(xor_1_out), .in5(multiplexer_2_out), .in6(or_2_out), .in7(and_2_out),
    .out(Result), .sel(ALUC));
  zero zero_1 (.Result(Result), .ZERO(sZero));
  // Probe on A
  // Probe on B

  // Other names for the same wires on the sheet: f7_5 = funct7[5]; op_5 = opcode[5]; Shift[4:0] = B[4:0]
endmodule
