// Logisim project zero.circ as structural Verilog: 1 circuit, main circuit zero
module zero (
  input  [31:0] Result,
  output ZERO
);

  Comparator #(.width(32)) comparator_1 (.a({32{1'b0}}), .b(Result), .eq(ZERO));  // open: gt, lt
endmodule
