// Logisim project bancoRegistradores.circ as structural Verilog: 1 circuit, main circuit bancoRegistradores
module bancoRegistradores (
  input  [31:0] WD,
  input  [4:0] WR,
  input  [4:0] LR1,
  input  [4:0] LR2,
  input  clk,
  input  RegWrite,
  output [31:0] LD1,
  output [31:0] LD2
);

  wire demultiplexer_2_out0, demultiplexer_2_out1, demultiplexer_2_out2, demultiplexer_2_out3,
       demultiplexer_2_out4, demultiplexer_2_out5, demultiplexer_2_out6, demultiplexer_2_out7,
       demultiplexer_2_out8, demultiplexer_2_out9, demultiplexer_2_out10, demultiplexer_2_out11,
       demultiplexer_2_out12, demultiplexer_2_out13, demultiplexer_2_out14, demultiplexer_2_out15,
       demultiplexer_2_out16, demultiplexer_2_out17, demultiplexer_2_out18, demultiplexer_2_out19,
       demultiplexer_2_out20, demultiplexer_2_out21, demultiplexer_2_out22, demultiplexer_2_out23,
       demultiplexer_2_out24, demultiplexer_2_out25, demultiplexer_2_out26, demultiplexer_2_out27,
       demultiplexer_2_out28, demultiplexer_2_out29, demultiplexer_2_out30, demultiplexer_2_out31;
  wire [31:0] demultiplexer_1_out0, demultiplexer_1_out1, demultiplexer_1_out2, demultiplexer_1_out3,
       demultiplexer_1_out4, demultiplexer_1_out5, demultiplexer_1_out6, demultiplexer_1_out7,
       demultiplexer_1_out8, demultiplexer_1_out9, demultiplexer_1_out10, demultiplexer_1_out11,
       demultiplexer_1_out12, demultiplexer_1_out13, demultiplexer_1_out14, demultiplexer_1_out15,
       demultiplexer_1_out16, demultiplexer_1_out17, demultiplexer_1_out18, demultiplexer_1_out19,
       demultiplexer_1_out20, demultiplexer_1_out21, demultiplexer_1_out22, demultiplexer_1_out23,
       demultiplexer_1_out24, demultiplexer_1_out25, demultiplexer_1_out26, demultiplexer_1_out27,
       demultiplexer_1_out28, demultiplexer_1_out29, demultiplexer_1_out30, demultiplexer_1_out31,
       register_1_q, register_2_q, register_3_q, register_4_q, register_5_q, register_6_q, register_7_q,
       register_8_q, register_9_q, register_10_q, register_11_q, register_12_q, register_13_q, register_14_q,
       register_15_q, register_16_q, register_17_q, register_18_q, register_19_q, register_20_q,
       register_21_q, register_22_q, register_23_q, register_24_q, register_25_q, register_26_q,
       register_27_q, register_28_q, register_29_q, register_30_q, register_31_q, register_32_q;

  // Probe on WD
  Demultiplexer #(.select(5), .width(32)) demultiplexer_1 (
    .out0(demultiplexer_1_out0), .out1(demultiplexer_1_out1), .out2(demultiplexer_1_out2),
    .out3(demultiplexer_1_out3), .out4(demultiplexer_1_out4), .out5(demultiplexer_1_out5),
    .out6(demultiplexer_1_out6), .out7(demultiplexer_1_out7), .out8(demultiplexer_1_out8),
    .out9(demultiplexer_1_out9), .out10(demultiplexer_1_out10), .out11(demultiplexer_1_out11),
    .out12(demultiplexer_1_out12), .out13(demultiplexer_1_out13), .out14(demultiplexer_1_out14),
    .out15(demultiplexer_1_out15), .out16(demultiplexer_1_out16), .out17(demultiplexer_1_out17),
    .out18(demultiplexer_1_out18), .out19(demultiplexer_1_out19), .out20(demultiplexer_1_out20),
    .out21(demultiplexer_1_out21), .out22(demultiplexer_1_out22), .out23(demultiplexer_1_out23),
    .out24(demultiplexer_1_out24), .out25(demultiplexer_1_out25), .out26(demultiplexer_1_out26),
    .out27(demultiplexer_1_out27), .out28(demultiplexer_1_out28), .out29(demultiplexer_1_out29),
    .out30(demultiplexer_1_out30), .out31(demultiplexer_1_out31), .in(WD), .sel(WR));
  Register #(.width(32)) register_1 (
    .D({32{1'b0}}), .en(demultiplexer_2_out0), .clk(clk), .Q(register_1_q));  // open: clr
  Register #(.width(32)) register_2 (
    .D(demultiplexer_1_out1), .en(demultiplexer_2_out1), .clk(clk), .Q(register_2_q));  // open: clr
  Register #(.width(32)) register_3 (
    .D(demultiplexer_1_out2), .en(demultiplexer_2_out2), .clk(clk), .Q(register_3_q));  // open: clr
  Register #(.width(32)) register_4 (
    .D(demultiplexer_1_out3), .en(demultiplexer_2_out3), .clk(clk), .Q(register_4_q));  // open: clr
  Register #(.width(32)) register_5 (
    .D(demultiplexer_1_out4), .en(demultiplexer_2_out4), .clk(clk), .Q(register_5_q));  // open: clr
  Register #(.width(32)) register_6 (
    .D(demultiplexer_1_out5), .en(demultiplexer_2_out5), .clk(clk), .Q(register_6_q));  // open: clr
  Register #(.width(32)) register_7 (
    .D(demultiplexer_1_out6), .en(demultiplexer_2_out6), .clk(clk), .Q(register_7_q));  // open: clr
  Register #(.width(32)) register_8 (
    .D(demultiplexer_1_out7), .en(demultiplexer_2_out7), .clk(clk), .Q(register_8_q));  // open: clr
  Register #(.width(32)) register_9 (
    .D(demultiplexer_1_out8), .en(demultiplexer_2_out8), .clk(clk), .Q(register_9_q));  // open: clr
  Register #(.width(32)) register_10 (
    .D(demultiplexer_1_out9), .en(demultiplexer_2_out9), .clk(clk), .Q(register_10_q));  // open: clr
  Register #(.width(32)) register_11 (
    .D(demultiplexer_1_out10), .en(demultiplexer_2_out10), .clk(clk), .Q(register_11_q));  // open: clr
  Register #(.width(32)) register_12 (
    .D(demultiplexer_1_out11), .en(demultiplexer_2_out11), .clk(clk), .Q(register_12_q));  // open: clr
  Register #(.width(32)) register_13 (
    .D(demultiplexer_1_out12), .en(demultiplexer_2_out12), .clk(clk), .Q(register_13_q));  // open: clr
  Register #(.width(32)) register_14 (
    .D(demultiplexer_1_out13), .en(demultiplexer_2_out13), .clk(clk), .Q(register_14_q));  // open: clr
  Register #(.width(32)) register_15 (
    .D(demultiplexer_1_out14), .en(demultiplexer_2_out14), .clk(clk), .Q(register_15_q));  // open: clr
  Register #(.width(32)) register_16 (
    .D(demultiplexer_1_out15), .en(demultiplexer_2_out15), .clk(clk), .Q(register_16_q));  // open: clr
  Register #(.width(32)) register_17 (
    .D(demultiplexer_1_out16), .en(demultiplexer_2_out16), .clk(clk), .Q(register_17_q));  // open: clr
  Register #(.width(32)) register_18 (
    .D(demultiplexer_1_out17), .en(demultiplexer_2_out17), .clk(clk), .Q(register_18_q));  // open: clr
  Register #(.width(32)) register_19 (
    .D(demultiplexer_1_out18), .en(demultiplexer_2_out18), .clk(clk), .Q(register_19_q));  // open: clr
  Register #(.width(32)) register_20 (
    .D(demultiplexer_1_out19), .en(demultiplexer_2_out19), .clk(clk), .Q(register_20_q));  // open: clr
  Register #(.width(32)) register_21 (
    .D(demultiplexer_1_out20), .en(demultiplexer_2_out20), .clk(clk), .Q(register_21_q));  // open: clr
  Register #(.width(32)) register_22 (
    .D(demultiplexer_1_out21), .en(demultiplexer_2_out21), .clk(clk), .Q(register_22_q));  // open: clr
  Register #(.width(32)) register_23 (
    .D(demultiplexer_1_out22), .en(demultiplexer_2_out22), .clk(clk), .Q(register_23_q));  // open: clr
  Register #(.width(32)) register_24 (
    .D(demultiplexer_1_out23), .en(demultiplexer_2_out23), .clk(clk), .Q(register_24_q));  // open: clr
  Register #(.width(32)) register_25 (
    .D(demultiplexer_1_out24), .en(demultiplexer_2_out24), .clk(clk), .Q(register_25_q));  // open: clr
  Register #(.width(32)) register_26 (
    .D(demultiplexer_1_out25), .en(demultiplexer_2_out25), .clk(clk), .Q(register_26_q));  // open: clr
  Register #(.width(32)) register_27 (
    .D(demultiplexer_1_out26), .en(demultiplexer_2_out26), .clk(clk), .Q(register_27_q));  // open: clr
  Register #(.width(32)) register_28 (
    .D(demultiplexer_1_out27), .en(demultiplexer_2_out27), .clk(clk), .Q(register_28_q));  // open: clr
  Register #(.width(32)) register_29 (
    .D(demultiplexer_1_out28), .en(demultiplexer_2_out28), .clk(clk), .Q(register_29_q));  // open: clr
  Register #(.width(32)) register_30 (
    .D(demultiplexer_1_out29), .en(demultiplexer_2_out29), .clk(clk), .Q(register_30_q));  // open: clr
  Register #(.width(32)) register_31 (
    .D(demultiplexer_1_out30), .en(demultiplexer_2_out30), .clk(clk), .Q(register_31_q));  // open: clr
  Register #(.width(32)) register_32 (
    .D(demultiplexer_1_out31), .en(demultiplexer_2_out31), .clk(clk), .Q(register_32_q));  // open: clr
  Demultiplexer #(.select(5)) demultiplexer_2 (
    .out0(demultiplexer_2_out0), .out1(demultiplexer_2_out1), .out2(demultiplexer_2_out2),
    .out3(demultiplexer_2_out3), .out4(demultiplexer_2_out4), .out5(demultiplexer_2_out5),
    .out6(demultiplexer_2_out6), .out7(demultiplexer_2_out7), .out8(demultiplexer_2_out8),
    .out9(demultiplexer_2_out9), .out10(demultiplexer_2_out10), .out11(demultiplexer_2_out11),
    .out12(demultiplexer_2_out12), .out13(demultiplexer_2_out13), .out14(demultiplexer_2_out14),
    .out15(demultiplexer_2_out15), .out16(demultiplexer_2_out16), .out17(demultiplexer_2_out17),
    .out18(demultiplexer_2_out18), .out19(demultiplexer_2_out19), .out20(demultiplexer_2_out20),
    .out21(demultiplexer_2_out21), .out22(demultiplexer_2_out22), .out23(demultiplexer_2_out23),
    .out24(demultiplexer_2_out24), .out25(demultiplexer_2_out25), .out26(demultiplexer_2_out26),
    .out27(demultiplexer_2_out27), .out28(demultiplexer_2_out28), .out29(demultiplexer_2_out29),
    .out30(demultiplexer_2_out30), .out31(demultiplexer_2_out31), .in(RegWrite), .sel(WR));
  Multiplexer #(.select(5), .width(32)) multiplexer_1 (
    .in0(register_1_q), .in1(register_2_q), .in2(register_3_q), .in3(register_4_q), .in4(register_5_q),
    .in5(register_6_q), .in6(register_7_q), .in7(register_8_q), .in8(register_9_q), .in9(register_10_q),
    .in10(register_11_q), .in11(register_12_q), .in12(register_13_q), .in13(register_14_q),
    .in14(register_15_q), .in15(register_16_q), .in16(register_17_q), .in17(register_18_q),
    .in18(register_19_q), .in19(register_20_q), .in20(register_21_q), .in21(register_22_q),
    .in22(register_23_q), .in23(register_24_q), .in24(register_25_q), .in25(register_26_q),
    .in26(register_27_q), .in27(register_28_q), .in28(register_29_q), .in29(register_30_q),
    .in30(register_31_q), .in31(register_32_q), .out(LD1), .sel(LR1));
  Multiplexer #(.select(5), .width(32)) multiplexer_2 (
    .in0(register_1_q), .in1(register_2_q), .in2(register_3_q), .in3(register_4_q), .in4(register_5_q),
    .in5(register_6_q), .in6(register_7_q), .in7(register_8_q), .in8(register_9_q), .in9(register_10_q),
    .in10(register_11_q), .in11(register_12_q), .in12(register_13_q), .in13(register_14_q),
    .in14(register_15_q), .in15(register_16_q), .in16(register_17_q), .in17(register_18_q),
    .in18(register_19_q), .in19(register_20_q), .in20(register_21_q), .in21(register_22_q),
    .in22(register_23_q), .in23(register_24_q), .in24(register_25_q), .in25(register_26_q),
    .in26(register_27_q), .in27(register_28_q), .in28(register_29_q), .in29(register_30_q),
    .in30(register_31_q), .in31(register_32_q), .out(LD2), .sel(LR2));

  // Notes on the sheet:
  //   x0
  //   x1
  //   x2
  //   x3
  //   x4
  //   x5
  //   x6
  //   x7
  //   x8
  //   x9
  //   x10
  //   x11
  //   x12
  //   x13
  //   x14
  //   x15
  //   x16
  //   x17
  //   x18
  //   x19
  //   x20
  //   x21
  //   x22
  //   x23
  //   x24
  //   x25
  //   x26
  //   x27
  //   x28
  //   x29
  //   x30
  //   x31
endmodule
