// Logisim project controleEnderecamento.circ as structural Verilog: 1 circuit, main circuit ucEnderecamento
module ucEnderecamento (
  input  [2:0] Funct3,
  input  writeEnable,
  input  [31:0] Adress,
  output [3:0] byteEnable,
  output [1:0] Size,
  output [1:0] Offset,
  output signal_unsigned
);

  wire [3:0] multiplexer_1_out, shifter_1_out;

  Multiplexer #(.select(2), .width(4)) multiplexer_1 (
    .in0(4'b0001), .in1(4'b0011), .in2(4'b1111), .out(multiplexer_1_out), .sel(Funct3[1:0]));  // open: in3
  Shifter #(.width(4)) shifter_1 (.in(multiplexer_1_out), .\dist (Adress[1:0]), .out(shifter_1_out));
  and and_1 (byteEnable[0], shifter_1_out[0], writeEnable);
  and and_2 (byteEnable[1], shifter_1_out[1], writeEnable);
  and and_3 (byteEnable[2], shifter_1_out[2], writeEnable);
  and and_4 (byteEnable[3], shifter_1_out[3], writeEnable);

  assign Offset = Adress[1:0];
  assign signal_unsigned = Funct3[2];
  assign Size = Funct3[1:0];

  // Notes on the sheet:
  //   0001
  //   0011
  //   1111
  //   0000
endmodule
