// Logisim project ID_EX_stage_bubble.circ as structural Verilog: 1 circuit, main circuit ID_EX_stage
module ID_EX_stage (
  input  [31:0] PCplus4_ID,
  input  [6:0] opcode_ID,
  input  RegWrite_ID,
  input  Lui_ID,
  input  [31:0] PC_ID,
  input  ALUSrcB_ID,
  input  MemToReg_ID,
  input  [31:0] ld1_ID,
  input  MemRead_ID,
  input  Jump_ID,
  input  [31:0] ld2_ID,
  input  [1:0] ALUOp_ID,
  input  MemWrite_ID,
  input  [4:0] rd_ID,
  input  Auipc_ID,
  input  [2:0] f3_ID,
  input  Jalr_ID,
  input  [6:0] f7_ID,
  input  CLK,
  input  [31:0] imm_ID,
  input  Clear,
  input  Enable,
  output [31:0] PCplus4_EX,
  output [6:0] opcode_EX,
  output RegWrite_EX,
  output Lui_EX,
  output [31:0] PC_EX,
  output ALUSrcB_EX,
  output MemToReg_EX,
  output [31:0] ld1_EX,
  output MemRead_EX,
  output Jump_EX,
  output [31:0] ld2_EX,
  output [1:0] ALUOp_EX,
  output MemWrite_EX,
  output [4:0] rd_EX,
  output Auipc_EX,
  output [2:0] f3_EX,
  output Jalr_EX,
  output [6:0] f7_EX,
  output [31:0] imm_EX
);

  wire multiplexer_10_out, multiplexer_11_out, multiplexer_12_out, multiplexer_14_out, multiplexer_15_out,
       multiplexer_16_out, multiplexer_17_out, multiplexer_18_out, multiplexer_19_out, undriven;
  wire [1:0] multiplexer_13_out;
  wire [2:0] multiplexer_7_out;
  wire [4:0] multiplexer_6_out;
  wire [6:0] multiplexer_3_out, multiplexer_8_out;
  wire [31:0] multiplexer_1_out, multiplexer_2_out, multiplexer_4_out, multiplexer_5_out, multiplexer_9_out;

  Multiplexer #(.width(32)) multiplexer_1 (.in0(PCplus4_ID), .in1({32{1'b0}}), .out(multiplexer_1_out), .sel(Clear));
  Multiplexer #(.width(32)) multiplexer_2 (.in0(PC_ID), .in1({32{1'b0}}), .out(multiplexer_2_out), .sel(Clear));
  Register #(.trigger("falling"), .width(32)) PCplus4 (
    .D(multiplexer_1_out), .en(Enable), .clk(CLK), .Q(PCplus4_EX));  // open: clr
  Register #(.trigger("falling"), .width(32)) PC (
    .D(multiplexer_2_out), .en(Enable), .clk(CLK), .Q(PC_EX));  // open: clr
  Multiplexer #(.width(7)) multiplexer_3 (.in0(opcode_ID), .in1(7'b0010011), .out(multiplexer_3_out), .sel(Clear));
  Multiplexer #(.width(32)) multiplexer_4 (.in0(ld1_ID), .in1({32{1'b0}}), .out(multiplexer_4_out), .sel(Clear));
  Multiplexer #(.width(32)) multiplexer_5 (.in0(ld2_ID), .in1({32{1'b0}}), .out(multiplexer_5_out), .sel(Clear));
  Multiplexer #(.width(5)) multiplexer_6 (.in0(rd_ID), .in1({5{1'b0}}), .out(multiplexer_6_out), .sel(Clear));
  Multiplexer #(.width(3)) multiplexer_7 (.in0(f3_ID), .in1(3'b000), .out(multiplexer_7_out), .sel(Clear));
  Multiplexer #(.width(7)) multiplexer_8 (.in0(f7_ID), .in1({7{1'b0}}), .out(multiplexer_8_out), .sel(Clear));
  Multiplexer #(.width(32)) multiplexer_9 (.in0(imm_ID), .in1({32{1'b0}}), .out(multiplexer_9_out), .sel(Clear));
  Register #(.trigger("falling"), .width(7)) opcode (
    .D(multiplexer_3_out), .en(Enable), .clk(CLK), .Q(opcode_EX));  // open: clr
  Register #(.trigger("falling"), .width(32)) ld1 (
    .D(multiplexer_4_out), .en(Enable), .clk(CLK), .Q(ld1_EX));  // open: clr
  Register #(.trigger("falling"), .width(32)) ld2 (
    .D(multiplexer_5_out), .en(Enable), .clk(CLK), .Q(ld2_EX));  // open: clr
  Register #(.trigger("falling"), .width(5)) rd (
    .D(multiplexer_6_out), .en(Enable), .clk(CLK), .Q(rd_EX));  // open: clr
  Register #(.trigger("falling"), .width(3)) funct3 (
    .D(multiplexer_7_out), .en(Enable), .clk(CLK), .Q(f3_EX), .clr(undriven));
  Register #(.trigger("falling"), .width(7)) funct7 (
    .D(multiplexer_8_out), .en(Enable), .clk(CLK), .Q(f7_EX));  // open: clr
  Register #(.trigger("falling"), .width(32)) imm (
    .D(multiplexer_9_out), .en(Enable), .clk(CLK), .Q(imm_EX));  // open: clr
  Multiplexer multiplexer_10 (.in0(RegWrite_ID), .in1(1'b0), .out(multiplexer_10_out), .sel(Clear));
  Multiplexer multiplexer_11 (.in0(ALUSrcB_ID), .in1(1'b0), .out(multiplexer_11_out), .sel(Clear));
  Multiplexer multiplexer_12 (.in0(Jump_ID), .in1(1'b0), .out(multiplexer_12_out), .sel(Clear));
  Multiplexer #(.width(2)) multiplexer_13 (.in0(ALUOp_ID), .in1(2'b00), .out(multiplexer_13_out), .sel(Clear));
  Multiplexer multiplexer_14 (.in0(Auipc_ID), .in1(1'b0), .out(multiplexer_14_out), .sel(Clear));
  Multiplexer multiplexer_15 (.in0(Jalr_ID), .in1(1'b0), .out(multiplexer_15_out), .sel(Clear));
  Register #(.trigger("falling"), .width(1)) RegWrite (
    .D(multiplexer_10_out), .en(Enable), .clk(CLK), .Q(RegWrite_EX));  // open: clr
  Register #(.trigger("falling"), .width(1)) ALUSrc (
    .D(multiplexer_11_out), .en(Enable), .clk(CLK), .Q(ALUSrcB_EX));  // open: clr
  Register #(.trigger("falling"), .width(1)) Jump (
    .D(multiplexer_12_out), .en(Enable), .clk(CLK), .Q(Jump_EX));  // open: clr
  Register #(.trigger("falling"), .width(2)) ALUOp (
    .D(multiplexer_13_out), .en(Enable), .clk(CLK), .Q(ALUOp_EX));  // open: clr
  Register #(.trigger("falling"), .width(1)) Auipc (
    .D(multiplexer_14_out), .en(Enable), .clk(CLK), .Q(Auipc_EX));  // open: clr
  Register #(.trigger("falling"), .width(1)) Jalr (
    .D(multiplexer_15_out), .en(Enable), .clk(CLK), .Q(Jalr_EX));  // open: clr
  Multiplexer multiplexer_16 (.in0(Lui_ID), .in1(1'b0), .out(multiplexer_16_out), .sel(Clear));
  Multiplexer multiplexer_17 (.in0(MemToReg_ID), .in1(1'b0), .out(multiplexer_17_out), .sel(Clear));
  Multiplexer multiplexer_18 (.in0(MemRead_ID), .in1(1'b0), .out(multiplexer_18_out), .sel(Clear));
  Multiplexer multiplexer_19 (.in0(MemWrite_ID), .in1(1'b0), .out(multiplexer_19_out), .sel(Clear));
  Register #(.trigger("falling"), .width(1)) Lui (
    .D(multiplexer_16_out), .en(Enable), .clk(CLK), .Q(Lui_EX));  // open: clr
  Register #(.trigger("falling"), .width(1)) MemToReg (
    .D(multiplexer_17_out), .en(Enable), .clk(CLK), .Q(MemToReg_EX));  // open: clr
  Register #(.trigger("falling"), .width(1)) MemRead (
    .D(multiplexer_18_out), .en(Enable), .clk(CLK), .Q(MemRead_EX));  // open: clr
  Register #(.trigger("falling"), .width(1)) MemWrite (
    .D(multiplexer_19_out), .en(Enable), .clk(CLK), .Q(MemWrite_EX));  // open: clr

  // Notes on the sheet:
  //   PC
  //   Decodificador
  //   ucPrincipal e ucDesvio
endmodule
