// Logisim project estagioEX_MEM.circ as structural Verilog: 1 circuit, main circuit estagioEX_MEM
module estagioEX_MEM (
  input  CLK,
  input  [31:0] ALUResult_EX,
  input  RegWrite_EX,
  input  MemRead_EX,
  input  [31:0] ld2_EX,
  input  MemToReg_EX,
  input  MemWrite_EX,
  input  [4:0] rd_EX,
  input  Jump_EX,
  input  [31:0] PCplus4_EX,
  input  [2:0] f3_EX,
  input  [31:0] Instrucao_EX,
  output [31:0] ALUResult_MEM,
  output RegWrite_MEM,
  output MemRead_MEM,
  output [31:0] ld2_MEM,
  output MemToReg_MEM,
  output MemWrite_MEM,
  output [4:0] rd_MEM,
  output Jump_MEM,
  output [31:0] PCplus4_MEM,
  output [2:0] f3_MEM,
  output [31:0] Instrucao_MEM
);

  Register #(.trigger("falling"), .width(32)) ALUResult (
    .D(ALUResult_EX), .en(1'b1), .clk(CLK), .Q(ALUResult_MEM), .clr(1'b0));
  Register #(.trigger("falling"), .width(32)) ld2 (.D(ld2_EX), .en(1'b1), .clk(CLK), .Q(ld2_MEM), .clr(1'b0));
  Register #(.trigger("falling"), .width(5)) rd (.D(rd_EX), .en(1'b1), .clk(CLK), .Q(rd_MEM), .clr(1'b0));
  Register #(.trigger("falling"), .width(32)) PCplus4 (
    .D(PCplus4_EX), .en(1'b1), .clk(CLK), .Q(PCplus4_MEM), .clr(1'b0));
  Register #(.trigger("falling"), .width(3)) f3 (.D(f3_EX), .en(1'b1), .clk(CLK), .Q(f3_MEM), .clr(1'b0));
  Register #(.trigger("falling"), .width(32)) Instrucao (
    .D(Instrucao_EX), .en(1'b1), .clk(CLK), .Q(Instrucao_MEM), .clr(1'b0));
  Register #(.trigger("falling"), .width(1)) MemRead (
    .D(MemRead_EX), .en(1'b1), .clk(CLK), .Q(MemRead_MEM), .clr(1'b0));
  Register #(.trigger("falling"), .width(1)) MemWrite (
    .D(MemWrite_EX), .en(1'b1), .clk(CLK), .Q(MemWrite_MEM), .clr(1'b0));
  Register #(.trigger("falling"), .width(1)) RegWrite (
    .D(RegWrite_EX), .en(1'b1), .clk(CLK), .Q(RegWrite_MEM), .clr(1'b0));
  Register #(.trigger("falling"), .width(1)) MemToReg (
    .D(MemToReg_EX), .en(1'b1), .clk(CLK), .Q(MemToReg_MEM), .clr(1'b0));
  Register #(.trigger("falling"), .width(1)) Jump (.D(Jump_EX), .en(1'b1), .clk(CLK), .Q(Jump_MEM), .clr(1'b0));

  // Notes on the sheet:
  //   Dados
  //   Controle MEM
  //   Controle WB
endmodule
