// Logisim project estagioID_EX.circ as structural Verilog: 1 circuit, main circuit estagioID_EX
module estagioID_EX (
  input  [31:0] PCplus4_ID,
  input  [6:0] opcode_ID,
  input  RegWrite_ID,
  input  Lui_ID,
  input  [31:0] PC_ID,
  input  [31:0] ld1_ID,
  input  ALUSrcB_ID,
  input  MemToReg_ID,
  input  [31:0] ld2_ID,
  input  MemRead_ID,
  input  Jump_ID,
  input  [4:0] rd_ID,
  input  [1:0] ALUOp_ID,
  input  MemWrite_ID,
  input  [31:0] Instrucao_ID,
  input  [2:0] f3_ID,
  input  Auipc_ID,
  input  [6:0] f7_ID,
  input  Jalr_ID,
  input  [31:0] imm_ID,
  input  CLK,
  input  [4:0] rs1_ID,
  input  [4:0] rs2_ID,
  output [31:0] PCplus4_EX,
  output [6:0] opcode_EX,
  output RegWrite_EX,
  output Lui_EX,
  output [31:0] PC_EX,
  output [31:0] ld1_EX,
  output ALUSrcB_EX,
  output MemToReg_EX,
  output [31:0] ld2_EX,
  output MemRead_EX,
  output Jump_EX,
  output [4:0] rd_EX,
  output [1:0] ALUOp_EX,
  output MemWrite_EX,
  output [31:0] Instrucao_EX,
  output [2:0] f3_EX,
  output Auipc_EX,
  output [6:0] f7_EX,
  output Jalr_EX,
  output [31:0] imm_EX,
  output [4:0] rs1_EX,
  output [4:0] rs2_EX
);

  Register #(.trigger("falling"), .width(32)) PCplus4 (
    .D(PCplus4_ID), .en(1'b1), .clk(CLK), .Q(PCplus4_EX), .clr(1'b0));
  Register #(.trigger("falling"), .width(32)) PC (.D(PC_ID), .en(1'b1), .clk(CLK), .Q(PC_EX), .clr(1'b0));
  Register #(.trigger("falling"), .width(32)) Instrucao (
    .D(Instrucao_ID), .en(1'b1), .clk(CLK), .Q(Instrucao_EX), .clr(1'b0));
  Register #(.trigger("falling"), .width(7)) opcode (.D(opcode_ID), .en(1'b1), .clk(CLK), .Q(opcode_EX), .clr(1'b0));
  Register #(.trigger("falling"), .width(32)) ld1 (.D(ld1_ID), .en(1'b1), .clk(CLK), .Q(ld1_EX));  // open: clr
  Register #(.trigger("falling"), .width(32)) ld2 (.D(ld2_ID), .en(1'b1), .clk(CLK), .Q(ld2_EX), .clr(1'b0));
  Register #(.trigger("falling"), .width(5)) rd (.D(rd_ID), .en(1'b1), .clk(CLK), .Q(rd_EX), .clr(1'b0));
  Register #(.trigger("falling"), .width(3)) funct3 (.D(f3_ID), .en(1'b1), .clk(CLK), .Q(f3_EX), .clr(1'b0));
  Register #(.trigger("falling"), .width(7)) funct7 (.D(f7_ID), .en(1'b1), .clk(CLK), .Q(f7_EX), .clr(1'b0));
  Register #(.trigger("falling"), .width(32)) imm (.D(imm_ID), .en(1'b1), .clk(CLK), .Q(imm_EX), .clr(1'b0));
  Register #(.trigger("falling"), .width(5)) rs1 (.D(rs1_ID), .en(1'b1), .clk(CLK), .Q(rs1_EX), .clr(1'b0));
  Register #(.trigger("falling"), .width(5)) rs2 (.D(rs2_ID), .en(1'b1), .clk(CLK), .Q(rs2_EX), .clr(1'b0));
  Register #(.trigger("falling"), .width(1)) RegWrite (
    .D(RegWrite_ID), .en(1'b1), .clk(CLK), .Q(RegWrite_EX), .clr(1'b0));
  Register #(.trigger("falling"), .width(1)) ALUSrc (.D(ALUSrcB_ID), .en(1'b1), .clk(CLK), .Q(ALUSrcB_EX), .clr(1'b0));
  Register #(.trigger("falling"), .width(1)) Jump (.D(Jump_ID), .en(1'b1), .clk(CLK), .Q(Jump_EX), .clr(1'b0));
  Register #(.trigger("falling"), .width(2)) ALUOp (.D(ALUOp_ID), .en(1'b1), .clk(CLK), .Q(ALUOp_EX), .clr(1'b0));
  Register #(.trigger("falling"), .width(1)) Auipc (.D(Auipc_ID), .en(1'b1), .clk(CLK), .Q(Auipc_EX), .clr(1'b0));
  Register #(.trigger("falling"), .width(1)) Jalr (.D(Jalr_ID), .en(1'b1), .clk(CLK), .Q(Jalr_EX), .clr(1'b0));
  Register #(.trigger("falling"), .width(1)) MemRead (.D(MemRead_ID), .en(1'b1), .clk(CLK), .Q(MemRead_EX), .clr(1'b0));
  Register #(.trigger("falling"), .width(1)) Lui (.D(Lui_ID), .en(1'b1), .clk(CLK), .Q(Lui_EX), .clr(1'b0));
  Register #(.trigger("falling"), .width(1)) MemToReg (
    .D(MemToReg_ID), .en(1'b1), .clk(CLK), .Q(MemToReg_EX), .clr(1'b0));
  Register #(.trigger("falling"), .width(1)) MemWrite (
    .D(MemWrite_ID), .en(1'b1), .clk(CLK), .Q(MemWrite_EX), .clr(1'b0));

  // Notes on the sheet:
  //   PC
  //   Instrução
  //   Decodificador
  //   ucPrincipal e ucDesvio
endmodule
