// Logisim project estagioIF_ID.circ as structural Verilog: 1 circuit, main circuit estagioIF_ID
module estagioIF_ID (
  input  CLK,
  input  Enable,
  input  [31:0] Instrucao_IF,
  input  [31:0] PCplus4_IF,
  input  [31:0] PC_IF,
  output [31:0] Instrucao_ID,
  output [31:0] PCplus4_ID,
  output [31:0] PC_ID
);

  Register #(.trigger("falling"), .width(32)) PCplus4 (
    .D(PCplus4_IF), .en(Enable), .clk(CLK), .Q(PCplus4_ID), .clr(1'b0));
  Register #(.trigger("falling"), .width(32)) PC (.D(PC_IF), .en(Enable), .clk(CLK), .Q(PC_ID), .clr(1'b0));
  Register #(.trigger("falling"), .width(32)) Instrucao (
    .D(Instrucao_IF), .en(Enable), .clk(CLK), .Q(Instrucao_ID), .clr(1'b0));
endmodule
