// Logisim project estagioMEM_WB.circ as structural Verilog: 1 circuit, main circuit estagioMEM_WB
module estagioMEM_WB (
  input  CLK,
  input  [31:0] MemData_MEM,
  input  RegWrite_MEM,
  input  [31:0] ALUResult_MEM,
  input  MemToReg_MEM,
  input  [4:0] rd_MEM,
  input  Jump_MEM,
  input  [31:0] PCplus4_MEM,
  input  [31:0] Instrucao_MEM,
  output [31:0] MemData_WB,
  output RegWrite_WB,
  output [31:0] ALUResult_WB,
  output MemToReg_WB,
  output [4:0] rd_WB,
  output Jump_WB,
  output [31:0] PCplus4_WB,
  output [31:0] Instrucao_WB
);

  Register #(.trigger("falling"), .width(32)) MemData (
    .D(MemData_MEM), .en(1'b1), .clk(CLK), .Q(MemData_WB), .clr(1'b0));
  Register #(.trigger("falling"), .width(32)) ALUResult (
    .D(ALUResult_MEM), .en(1'b1), .clk(CLK), .Q(ALUResult_WB), .clr(1'b0));
  Register #(.trigger("falling"), .width(5)) rd (.D(rd_MEM), .en(1'b1), .clk(CLK), .Q(rd_WB), .clr(1'b0));
  Register #(.trigger("falling"), .width(32)) PCplus4 (
    .D(PCplus4_MEM), .en(1'b1), .clk(CLK), .Q(PCplus4_WB), .clr(1'b0));
  Register #(.trigger("falling"), .width(32)) Instrucao (
    .D(Instrucao_MEM), .en(1'b1), .clk(CLK), .Q(Instrucao_WB), .clr(1'b0));
  Register #(.trigger("falling"), .width(1)) RegWrite (
    .D(RegWrite_MEM), .en(1'b1), .clk(CLK), .Q(RegWrite_WB), .clr(1'b0));
  Register #(.trigger("falling"), .width(1)) MemToReg (
    .D(MemToReg_MEM), .en(1'b1), .clk(CLK), .Q(MemToReg_WB), .clr(1'b0));
  Register #(.trigger("falling"), .width(1)) Jump (.D(Jump_MEM), .en(1'b1), .clk(CLK), .Q(Jump_WB), .clr(1'b0));

  // Notes on the sheet:
  //   Dados
  //   Controle WB
endmodule
