// Logisim project memdados.circ as structural Verilog: 1 circuit, main circuit memDados
module memDados (
  input  [31:0] Endereco,
  input  clk,
  input  MemRead,
  input  [3:0] byteEnable,
  input  [31:0] dado,
  input  [1:0] size,
  input  [1:0] offset,
  input  sUnsigned,
  output [31:0] Dados_lidos
);

  wire [7:0] banco0_dout, multiplexer_2_out, ram_1_dout, ram_2_dout, ram_3_dout;
  wire [15:0] multiplexer_4_out;
  wire [31:0] extensorsinal_8_1_p2, extensorsinal_16_1_p2, extensorzero_8_1_p2, extensorzero_16_1_p2,
       multiplexer_1_out, multiplexer_3_out, multiplexer_5_out;

  Multiplexer #(.select(2), .width(32)) multiplexer_1 (
    .in0({dado[7:0], dado[7:0], dado[7:0], dado[7:0]}), .in1({dado[15:0], dado[15:0]}), .in2(dado),
    .out(multiplexer_1_out), .sel(size));  // open: in3
  RAM #(.addrWidth(24), .trigger("falling")) banco0 (
    .addr(Endereco[25:2]), .we(byteEnable[0]), .oe(MemRead), .clk(clk), .din(multiplexer_1_out[7:0]),
    .dout(banco0_dout));
  Multiplexer #(.select(2), .width(8)) multiplexer_2 (
    .in0(banco0_dout), .in1(ram_1_dout), .in2(ram_2_dout), .in3(ram_3_dout), .out(multiplexer_2_out),
    .sel(Endereco[1:0]));
  // extensorSinal_8 extensorsinal_8_1: pin names not known; wires that end beside it: multiplexer_2_out, extensorsinal_8_1_p2
  // extensorZero_8 extensorzero_8_1: pin names not known; wires that end beside it: multiplexer_2_out, extensorzero_8_1_p2
  RAM #(.addrWidth(24), .trigger("falling")) ram_1 (
    .addr(Endereco[25:2]), .we(byteEnable[1]), .oe(MemRead), .clk(clk), .din(multiplexer_1_out[15:8]),
    .dout(ram_1_dout));
  Multiplexer #(.width(32)) multiplexer_3 (
    .in0(extensorsinal_8_1_p2), .in1(extensorzero_8_1_p2), .out(multiplexer_3_out), .sel(sUnsigned));
  Multiplexer #(.width(16)) multiplexer_4 (
    .in0({ram_1_dout, banco0_dout}), .in1({ram_3_dout, ram_2_dout}), .out(multiplexer_4_out),
    .sel(Endereco[1]));
  // extensorSinal_16 extensorsinal_16_1: pin names not known; wires that end beside it: multiplexer_4_out, extensorsinal_16_1_p2
  // extensorZero_16 extensorzero_16_1: pin names not known; wires that end beside it: multiplexer_4_out, extensorzero_16_1_p2
  Multiplexer #(.width(32)) multiplexer_5 (
    .in0(extensorsinal_16_1_p2), .in1(extensorzero_16_1_p2), .out(multiplexer_5_out), .sel(sUnsigned));
  RAM #(.addrWidth(24), .trigger("falling")) ram_2 (
    .addr(Endereco[25:2]), .we(byteEnable[2]), .oe(MemRead), .clk(clk), .din(multiplexer_1_out[23:16]),
    .dout(ram_2_dout));
  Multiplexer #(.select(2), .width(32)) multiplexer_6 (
    .in0(multiplexer_3_out), .in1(multiplexer_5_out),
    .in2({ram_3_dout, ram_2_dout, ram_1_dout, banco0_dout}), .out(Dados_lidos), .sel(size));  // open: in3
  RAM #(.addrWidth(24), .trigger("falling")) ram_3 (
    .addr(Endereco[25:2]), .we(byteEnable[3]), .oe(MemRead), .clk(clk), .din(multiplexer_1_out[31:24]),
    .dout(ram_3_dout));

  assign offset = Endereco[1:0];
endmodule
