// Logisim project overflow.circ as structural Verilog: 1 circuit, main circuit overflow
module overflow (
  input  [31:0] a,
  input  [31:0] b,
  input  [31:0] Result,
  input  [3:0] Operador,
  output out_5
);

  wire and_1_out, and_2_out, and_3_out, and_4_out, and_5_out, and_6_out;

  and and_1 (and_1_out, Operador[0], ~Operador[1], Operador[2], ~Operador[3]);  // AND_Gate
  and and_2 (and_2_out, ~Operador[0], Operador[1], Operador[2], ~Operador[3]);  // AND_Gate
  and and_3 (and_3_out, Result[31], ~b[31], ~a[31], and_1_out);  // AND_Gate
  and and_4 (and_4_out, ~Result[31], b[31], a[31], and_1_out);  // AND_Gate
  and and_5 (and_5_out, Result[31], b[31], ~a[31], and_2_out);  // AND_Gate
  and and_6 (and_6_out, ~Result[31], ~b[31], a[31], and_2_out);  // AND_Gate
  or or_1 (out_5, and_3_out, and_4_out, and_5_out, and_6_out);
endmodule
