// Logisim project hazard_detection_unit.circ as structural Verilog: 1 circuit, main circuit hazard_detection_unit
module hazard_detection_unit (
  input  [4:0] rs1_ID,
  input  read_rs1,
  input  [4:0] rs2_ID,
  input  read_rs2,
  input  [4:0] rd_EX,
  input  RegWrite_EX,
  input  [4:0] rd_MEM,
  input  RegWrite_MEM,
  input  Jalr_EX,
  input  PCSrc_ID,
  input  [4:0] rd_WB,
  input  RegWrite_WB,
  output Stall,
  output Flush_IF,
  output Redirect_ID,
  output Bubble_ID
);

  wire and_1_out, and_2_out, and_3_out, and_4_out, and_5_out, and_6_out, and_7_out, and_8_out, and_9_out,
       comparator_1_eq, comparator_2_eq, comparator_3_gt, comparator_4_eq, comparator_5_eq, comparator_6_gt,
       comparator_7_eq, comparator_8_eq, comparator_9_gt, EX_out, MEM_out, or_1_out, or_2_out, or_3_out,
       WB_out;

  Comparator #(.mode("unsigned"), .width(5)) comparator_1 (
    .a(rs1_ID), .b(rd_EX), .eq(comparator_1_eq));  // open: gt, lt
  Comparator #(.mode("unsigned"), .width(5)) comparator_2 (
    .a(rs2_ID), .b(rd_EX), .eq(comparator_2_eq));  // open: gt, lt
  Comparator #(.mode("unsigned"), .width(5)) comparator_3 (
    .a(rd_EX), .b({5{1'b0}}), .gt(comparator_3_gt));  // open: eq, lt
  Comparator #(.mode("unsigned"), .width(5)) comparator_4 (
    .a(rs1_ID), .b(rd_MEM), .eq(comparator_4_eq));  // open: gt, lt
  Comparator #(.mode("unsigned"), .width(5)) comparator_5 (
    .a(rs2_ID), .b(rd_MEM), .eq(comparator_5_eq));  // open: gt, lt
  Comparator #(.mode("unsigned"), .width(5)) comparator_6 (
    .a(rd_MEM), .b({5{1'b0}}), .gt(comparator_6_gt));  // open: eq, lt
  Comparator #(.mode("unsigned"), .width(5)) comparator_7 (
    .a(rs1_ID), .b(rd_WB), .eq(comparator_7_eq));  // open: gt, lt
  Comparator #(.mode("unsigned"), .width(5)) comparator_8 (
    .a(rs2_ID), .b(rd_WB), .eq(comparator_8_eq));  // open: gt, lt
  Comparator #(.mode("unsigned"), .width(5)) comparator_9 (
    .a(rd_WB), .b({5{1'b0}}), .gt(comparator_9_gt));  // open: eq, lt
  and and_1 (and_1_out, read_rs1, comparator_1_eq);
  and and_2 (and_2_out, read_rs2, comparator_2_eq);
  and and_3 (and_3_out, read_rs1, comparator_4_eq);
  and and_4 (and_4_out, read_rs2, comparator_5_eq);
  and and_5 (and_5_out, read_rs1, comparator_7_eq);
  and and_6 (and_6_out, read_rs2, comparator_8_eq);
  or or_1 (or_1_out, and_1_out, and_2_out);
  or or_2 (or_2_out, and_3_out, and_4_out);
  or or_3 (or_3_out, and_5_out, and_6_out);
  and and_7 (and_7_out, or_1_out, comparator_3_gt);
  and and_8 (and_8_out, or_2_out, comparator_6_gt);
  and and_9 (and_9_out, or_3_out, comparator_9_gt);
  and EX (EX_out, and_7_out, RegWrite_EX);
  and MEM (MEM_out, and_8_out, RegWrite_MEM);
  and WB (WB_out, and_9_out, RegWrite_WB);
  or or_4 (Stall, EX_out, MEM_out, WB_out);
  and and_10 (Redirect_ID, PCSrc_ID, ~Stall, ~Jalr_EX);  // AND_Gate
  or or_5 (Bubble_ID, Stall, Jalr_EX);
  or or_6 (Flush_IF, Jalr_EX, Redirect_ID);
endmodule
