// Logisim project ucBolhas.circ as structural Verilog: 1 circuit, main circuit ucBolhas
module ucBolhas (
  input  [4:0] rs1_ID,
  input  [4:0] rs2_ID,
  input  [4:0] rd_EX,
  input  RegWrite_EX,
  input  [4:0] rd_MEM,
  input  RegWrite_MEM,
  input  [4:0] rd_WB,
  input  RegWrite_WB,
  input  PCSrc,
  output Stall,
  output Flush
);

  wire comparator_1_eq, comparator_2_eq, comparator_3_gt, comparator_4_eq, comparator_5_eq, comparator_6_gt,
       comparator_7_eq, comparator_8_eq, comparator_9_gt, EX_out, MEM_out, or_1_out, or_2_out, or_3_out,
       WB_out;

  Comparator #(.mode("unsigned"), .width(5)) comparator_1 (
    .a(rs1_ID), .b(rd_EX), .eq(comparator_1_eq));  // open: gt, lt
  Comparator #(.mode("unsigned"), .width(5)) comparator_2 (
    .a(rs2_ID), .b(rd_EX), .eq(comparator_2_eq));  // open: gt, lt
  Comparator #(.mode("unsigned"), .width(5)) comparator_3 (
    .a(rd_EX), .b({5{1'b0}}), .gt(comparator_3_gt));  // open: eq, lt
  Comparator #(.mode("unsigned"), .width(5)) comparator_4 (
    .a(rs1_ID), .b(rd_MEM), .eq(comparator_4_eq));  // open: gt, lt
  Comparator #(.mode("unsigned"), .width(5)) comparator_5 (
    .a(rs2_ID), .b(rd_MEM), .eq(comparator_5_eq));  // open: gt, lt
  Comparator #(.mode("unsigned"), .width(5)) comparator_6 (
    .a(rd_MEM), .b({5{1'b0}}), .gt(comparator_6_gt));  // open: eq, lt
  Comparator #(.mode("unsigned"), .width(5)) comparator_7 (
    .a(rs1_ID), .b(rd_WB), .eq(comparator_7_eq));  // open: gt, lt
  Comparator #(.mode("unsigned"), .width(5)) comparator_8 (
    .a(rs2_ID), .b(rd_WB), .eq(comparator_8_eq));  // open: gt, lt
  Comparator #(.mode("unsigned"), .width(5)) comparator_9 (
    .a(rd_WB), .b({5{1'b0}}), .gt(comparator_9_gt));  // open: eq, lt
  or or_1 (or_1_out, comparator_1_eq, comparator_2_eq);
  or or_2 (or_2_out, comparator_4_eq, comparator_5_eq);
  or or_3 (or_3_out, comparator_7_eq, comparator_8_eq);
  and EX (EX_out, or_1_out, comparator_3_gt, RegWrite_EX);
  and MEM (MEM_out, or_2_out, comparator_6_gt, RegWrite_MEM);
  and WB (WB_out, or_3_out, comparator_9_gt, RegWrite_WB);
  or or_4 (Stall, EX_out, MEM_out, WB_out);
  and and_1 (Flush, PCSrc, ~Stall);  // AND_Gate

  // Notes on the sheet:
  //   rs1_ID == rd_WB
  //   rs1_ID == rd_EX
  //   rs1_ID == rd_MEM
  //   rd_EX != x0
  //   rd_MEM != x0
  //   rd_WB != x0
  //   Flush = PCSrc . !Stall
endmodule
