// Logisim project ucConflitos.circ as structural Verilog: 1 circuit, main circuit ucConflitos
module ucConflitos (
  input  [4:0] rs1_ID,
  input  read_rs1,
  input  [4:0] rs2_ID,
  input  read_rs2,
  input  [4:0] rd_EX,
  input  RegWrite_EX,
  input  [4:0] rd_MEM,
  input  RegWrite_MEM,
  input  PCSrc,
  output Stall,
  output Flush_ID,
  output Flush_IF
);

  wire and_1_out, and_2_out, and_3_out, and_4_out, and_5_out, and_6_out, comparator_1_eq, comparator_2_eq,
       comparator_3_gt, comparator_4_eq, comparator_5_eq, comparator_6_gt, EX_out, MEM_out, not_1_out,
       not_2_out, or_1_out, or_2_out;

  Comparator #(.mode("unsigned"), .width(5)) comparator_1 (
    .a(rs1_ID), .b(rd_EX), .eq(comparator_1_eq));  // open: gt, lt
  Comparator #(.mode("unsigned"), .width(5)) comparator_2 (
    .a(rs2_ID), .b(rd_EX), .eq(comparator_2_eq));  // open: gt, lt
  Comparator #(.mode("unsigned"), .width(5)) comparator_3 (
    .a(rd_EX), .b({5{1'b0}}), .gt(comparator_3_gt));  // open: eq, lt
  Comparator #(.mode("unsigned"), .width(5)) comparator_4 (
    .a(rs1_ID), .b(rd_MEM), .eq(comparator_4_eq));  // open: gt, lt
  Comparator #(.mode("unsigned"), .width(5)) comparator_5 (
    .a(rs2_ID), .b(rd_MEM), .eq(comparator_5_eq));  // open: gt, lt
  Comparator #(.mode("unsigned"), .width(5)) comparator_6 (
    .a(rd_MEM), .b({5{1'b0}}), .gt(comparator_6_gt));  // open: eq, lt
  and and_1 (and_1_out, read_rs1, comparator_1_eq);
  and and_2 (and_2_out, read_rs2, comparator_2_eq);
  or or_1 (or_1_out, and_1_out, and_2_out);
  not not_1 (not_1_out, comparator_3_gt);
  and and_3 (and_3_out, read_rs1, comparator_4_eq);
  and and_4 (and_4_out, read_rs2, comparator_5_eq);
  or or_2 (or_2_out, and_3_out, and_4_out);
  not not_2 (not_2_out, comparator_6_gt);
  and and_5 (and_5_out, or_1_out, not_1_out);
  and and_6 (and_6_out, or_2_out, not_2_out);
  and EX (EX_out, and_5_out, RegWrite_EX);
  and and_7 (Flush_IF, ~Flush_ID, PCSrc);  // AND_Gate
  and MEM (MEM_out, and_6_out, RegWrite_MEM);
  or or_3 (Flush_ID, EX_out, MEM_out);

  assign Stall = Flush_ID;
endmodule
