// Logisim project ucEncaminhamento.circ as structural Verilog: 1 circuit, main circuit ucEncaminhamento
module ucEncaminhamento (
  input  [4:0] rs1_ID,
  input  [4:0] rs2_ID,
  input  [4:0] rs1_EX,
  input  [4:0] rs2_EX,
  input  [4:0] rd_MEM,
  input  RegWrite_MEM,
  input  [4:0] rd_WB,
  input  RegWrite_WB,
  output [1:0] ForwardA_ID,
  output [1:0] ForwardB_ID,
  output [1:0] ForwardA_EX,
  output [1:0] ForwardB_EX
);

  wire comparator_1_eq, comparator_2_eq, comparator_3_eq, comparator_4_eq, comparator_5_eq, comparator_6_eq,
       comparator_7_eq, comparator_8_eq, comparator_9_eq, comparator_10_eq, escreveMEM, escreveWB;

  Comparator #(.width(5)) comparator_1 (.a(rd_MEM), .b({5{1'b0}}), .eq(comparator_1_eq));  // open: gt, lt
  Comparator #(.width(5)) comparator_2 (.a(rd_WB), .b({5{1'b0}}), .eq(comparator_2_eq));  // open: gt, lt
  and and_1 (escreveMEM, RegWrite_MEM, ~comparator_1_eq);  // AND_Gate
  and and_2 (escreveWB, RegWrite_WB, ~comparator_2_eq);  // AND_Gate
  Comparator #(.width(5)) comparator_3 (.a(rd_MEM), .b(rs1_ID), .eq(comparator_3_eq));  // open: gt, lt
  Comparator #(.width(5)) comparator_4 (.a(rd_MEM), .b(rs2_ID), .eq(comparator_4_eq));  // open: gt, lt
  Comparator #(.width(5)) comparator_5 (.a(rd_MEM), .b(rs1_EX), .eq(comparator_5_eq));  // open: gt, lt
  Comparator #(.width(5)) comparator_6 (.a(rd_MEM), .b(rs2_EX), .eq(comparator_6_eq));  // open: gt, lt
  and and_3 (ForwardA_ID[1], escreveMEM, comparator_3_eq);
  and and_4 (ForwardB_ID[1], escreveMEM, comparator_4_eq);
  and and_5 (ForwardA_EX[1], escreveMEM, comparator_5_eq);
  and and_6 (ForwardB_EX[1], escreveMEM, comparator_6_eq);
  Comparator #(.width(5)) comparator_7 (.a(rd_WB), .b(rs1_ID), .eq(comparator_7_eq));  // open: gt, lt
  Comparator #(.width(5)) comparator_8 (.a(rd_WB), .b(rs2_ID), .eq(comparator_8_eq));  // open: gt, lt
  Comparator #(.width(5)) comparator_9 (.a(rd_WB), .b(rs1_EX), .eq(comparator_9_eq));  // open: gt, lt
  Comparator #(.width(5)) comparator_10 (.a(rd_WB), .b(rs2_EX), .eq(comparator_10_eq));  // open: gt, lt
  and and_7 (ForwardA_ID[0], escreveWB, comparator_7_eq, ~ForwardA_ID[1]);  // AND_Gate
  and and_8 (ForwardB_ID[0], escreveWB, comparator_8_eq, ~ForwardB_ID[1]);  // AND_Gate
  and and_9 (ForwardA_EX[0], escreveWB, comparator_9_eq, ~ForwardA_EX[1]);  // AND_Gate
  and and_10 (ForwardB_EX[0], escreveWB, comparator_10_eq, ~ForwardB_EX[1]);  // AND_Gate

  // Other names for the same wires on the sheet: memA_EX = ForwardA_EX[0]; exA_EX = ForwardA_EX[1];
  //   memA_ID = ForwardA_ID[0]; exA_ID = ForwardA_ID[1]; memB_EX = ForwardB_EX[0]; exB_EX = ForwardB_EX[1];
  //   memB_ID = ForwardB_ID[0]; exB_ID = ForwardB_ID[1]

  // Notes on the sheet:
  //   Entradas
  //   Escrita válida
  //   Conflito no EX
  //   Conflito no MEM
  //   Saídas
endmodule
