// Logisim project ucBranch.circ as structural Verilog: 1 circuit, main circuit main
module main (
  input  Zero,
  input  Neg,
  input  LessUnsigned,
  input  [2:0] funct3,
  output BranchSrc
);

  wire and_1_out, and_2_out, and_3_out, and_4_out, and_5_out, and_6_out, beq_out, bge_out, bgeu_out, blt_out,
       bltu_out, bne_out;

  and beq (beq_out, ~funct3[2], ~funct3[1], ~funct3[0]);  // AND_Gate
  and and_1 (and_1_out, beq_out, Zero);
  and bne (bne_out, ~funct3[2], ~funct3[1], funct3[0]);  // AND_Gate
  and and_2 (and_2_out, bne_out, ~Zero);  // AND_Gate
  and blt (blt_out, funct3[2], ~funct3[1], ~funct3[0]);  // AND_Gate
  and and_3 (and_3_out, blt_out, Neg);
  or or_1 (BranchSrc, and_1_out, and_2_out, and_3_out, and_4_out, and_5_out, and_6_out);
  and bltu (bltu_out, funct3[2], funct3[1], ~funct3[0]);  // AND_Gate
  and and_4 (and_4_out, bltu_out, LessUnsigned);
  and bge (bge_out, funct3[2], ~funct3[1], funct3[0]);  // AND_Gate
  and and_5 (and_5_out, bge_out, ~Neg);  // AND_Gate
  and bgeu (bgeu_out, funct3[2], funct3[1], funct3[0]);
  and and_6 (and_6_out, bgeu_out, ~LessUnsigned);  // AND_Gate

  // Other names for the same wires on the sheet: LessU = LessUnsigned
endmodule
