// Logisim project control_unit_bubble.circ as structural Verilog: 1 circuit, main circuit control_unit
module control_unit (
  input  [6:0] opcode,
  input  BranchSrc,
  output RegWrite,
  output ALUSrcB,
  output PCSrc,
  output Jump,
  output S_Jalr,
  output [1:0] ALUOp,
  output Auipc_uc,
  output Lui_uc,
  output MemToReg,
  output MemRead,
  output MemWrite,
  output Branch,
  output read_rs2,
  output read_rs1,
  output Stop
);

  wire and_1_out, E, Itype, Jal, Rtype;

  and R (Rtype, opcode[0], opcode[1], ~opcode[2], ~opcode[3], opcode[4], opcode[5], ~opcode[6]);  // AND_Gate
  and I (Itype, opcode[0], opcode[1], ~opcode[2], ~opcode[3], opcode[4], ~opcode[5], ~opcode[6]);  // AND_Gate
  and Load (MemRead, opcode[0], opcode[1], ~opcode[2], ~opcode[3], ~opcode[4], ~opcode[5], ~opcode[6]);  // AND_Gate
  and S (MemWrite, opcode[0], opcode[1], ~opcode[2], ~opcode[3], ~opcode[4], opcode[5], ~opcode[6]);  // AND_Gate
  and B (ALUOp[0], opcode[0], opcode[1], ~opcode[2], ~opcode[3], ~opcode[4], opcode[5], opcode[6]);  // AND_Gate
  and u_Jal (Jal, opcode[0], opcode[1], opcode[2], opcode[3], ~opcode[4], opcode[5], opcode[6]);  // AND_Gate
  and Jalr (S_Jalr, opcode[0], opcode[1], opcode[2], ~opcode[3], ~opcode[4], opcode[5], opcode[6]);  // AND_Gate
  and Lui (Lui_uc, opcode[0], opcode[1], opcode[2], ~opcode[3], opcode[4], opcode[5], ~opcode[6]);  // AND_Gate
  and Auipc (Auipc_uc, opcode[0], opcode[1], opcode[2], ~opcode[3], opcode[4], ~opcode[5], ~opcode[6]);  // AND_Gate
  and u_E (E, opcode[0], opcode[1], ~opcode[2], ~opcode[3], opcode[4], opcode[5], opcode[6]);  // AND_Gate
  or or_1 (ALUOp[1], Rtype, Itype);
  or or_2 (RegWrite, Lui_uc, Jal, S_Jalr, MemRead, Itype, Rtype, Auipc_uc);
  or or_3 (ALUSrcB, Lui_uc, MemWrite, S_Jalr, MemRead, Itype, Auipc_uc);
  nor nor_1 (Stop, Rtype, Itype, MemRead, MemWrite, ALUOp[0], Jal, S_Jalr, Lui_uc, Auipc_uc, E);
  and and_1 (and_1_out, ALUOp[0], BranchSrc);
  or or_4 (PCSrc, Jal, and_1_out);
  or or_5 (Jump, Jal, S_Jalr);
  or or_6 (read_rs2, Rtype, MemWrite, ALUOp[0]);
  or or_7 (read_rs1, read_rs2, Itype, MemRead, S_Jalr);

  assign Branch = ALUOp[0];
  assign MemToReg = MemRead;

  // Other names for the same wires on the sheet: Btype = ALUOp[0]; Auipc = Auipc_uc; Jalr = S_Jalr; Load = MemRead;
  //   Lui = Lui_uc; Stype = MemWrite

  // Notes on the sheet:
  //   0110011
  //   0010011
  //   0000011
  //   0100011
  //   1100011
  //   1101111
  //   1100111
  //   0110111
  //   1100111
  //   1110011
endmodule
