// Logisim project ucULA.circ as structural Verilog: 1 circuit, main circuit ucULA
module ucULA (
  input  [6:0] funct7,
  input  [1:0] ALUOp,
  input  [2:0] funct3,
  output [3:0] ALUControl
);

  wire and_1_out, and_2_out;
  wire [3:0] multiplexer_1_out, multiplexer_2_out, multiplexer_3_out, multiplexer_4_out, undriven;

  and and_1 (and_1_out, funct7[5], ~funct7[4]);  // AND_Gate
  Multiplexer #(.width(4)) multiplexer_1 (.in0(4'b0010), .in1(4'b0110), .out(multiplexer_1_out), .sel(and_1_out));
  Multiplexer #(.width(4)) multiplexer_2 (.in0(4'b1000), .in1(4'b0101), .out(multiplexer_2_out), .sel(funct7[5]));
  Multiplexer #(.select(3), .width(4)) multiplexer_3 (
    .in0(multiplexer_1_out), .in1(4'b0111), .in2(4'b0100), .in3(4'b1010), .in4(4'b0011),
    .in5(multiplexer_2_out), .in6(4'b0001), .in7(4'b0000), .out(multiplexer_3_out), .sel(funct3));
  and and_2 (and_2_out, funct3[2], funct3[1]);
  Multiplexer #(.width(4)) multiplexer_4 (.in0(4'b0110), .in1(4'b1010), .out(multiplexer_4_out), .sel(and_2_out));
  Multiplexer #(.select(2), .width(4)) multiplexer_5 (
    .in0(4'b0010), .in1(multiplexer_4_out), .in2(multiplexer_3_out), .in3(undriven), .out(ALUControl),
    .sel(ALUOp));

  // Other names for the same wires on the sheet: f3[2:0] = funct3

  // Notes on the sheet:
  //   add
  //   sub
  //   srl/srli
  //   sra/srai
  //   imm[5:11] = 0x20
  //   sll/slli
  //   slt/slti
  //   sltu/sltiu
  //   xor/xori
  //   or/ori
  //   and/andi
  //   Rtype_Itype
  //   lw/sw
  //   Btype
endmodule
