// Logisim project ucULA.circ as structural Verilog: 1 circuit, main circuit ucULA
module ucULA (
  input  [6:0] funct7,
  input  [6:0] opcode,
  input  [1:0] ALUOp,
  input  [2:0] funct3,
  output [3:0] ALUControl
);

  wire and_1_out;
  wire [3:0] multiplexer_1_out, multiplexer_2_out, multiplexer_3_out, multiplexer_4_out, multiplexer_5_out;

  and and_1 (and_1_out, opcode[5], funct7[5]);
  Multiplexer #(.width(4)) multiplexer_1 (.in0(4'b0010), .in1(4'b0110), .out(multiplexer_1_out), .sel(and_1_out));
  Multiplexer #(.width(4)) multiplexer_2 (.in0(4'b1000), .in1(4'b0101), .out(multiplexer_2_out), .sel(funct7[5]));
  Multiplexer #(.select(3), .width(4)) multiplexer_3 (
    .in0(multiplexer_1_out), .in1(4'b0111), .in2(4'b0100), .in3(4'b1010), .in4(4'b0011),
    .in5(multiplexer_2_out), .in6(4'b0001), .in7(4'b0000), .out(multiplexer_3_out), .sel(funct3));
  Multiplexer #(.width(4)) multiplexer_4 (.in0(4'b0100), .in1(4'b1010), .out(multiplexer_4_out), .sel(funct3[1]));
  Multiplexer #(.width(4)) multiplexer_5 (
    .in0(4'b0110), .in1(multiplexer_4_out), .out(multiplexer_5_out), .sel(funct3[2]));
  Multiplexer #(.select(2), .width(4)) multiplexer_6 (
    .in0(4'b0010), .in1(multiplexer_5_out), .in2(multiplexer_3_out), .out(ALUControl), .sel(ALUOp));  // open: in3

  // Notes on the sheet:
  //   imm[5:11] = 0x20
  //   add/addi
  //   sub
  //   srl/srli
  //   sra/srai
  //   0x0
  //   0x5
  //   sll/slli
  //   slt/slti
  //   sltu/sltiu
  //   xor/xori
  //   or/ori
  //   and/andi
  //   0x7
  //   blt/bge
  //   bltu/bgeu
  //   funct3 >= 0x4
  //   beq/bne
  //   R-type/I-type
  //   lw/sw
  //   B-type
endmodule
