// Logisim project ula.circ as structural Verilog: 1 circuit, main circuit ULA
module ULA (
  input  [31:0] A,
  input  [31:0] B,
  input  [3:0] ALUControl,
  output sZero,
  output [31:0] Result
);

  wire comparator_1_lt, comparator_2_gt, comparator_3_lt, comparator_4_gt;
  wire [31:0] adder_1_out, and_1_out, extensorsinal_1_1_p2, extensorsinal_1_2_p2, extensorsinal_1_3_p2,
       extensorsinal_1_4_p2, or_1_out, shifter_1_out, shifter_2_out, shifter_3_out, subtractor_1_out,
       xor_1_out;

  // Probe on A
  // Probe on B
  Comparator #(.width(32)) comparator_1 (.a(A), .b(B), .lt(comparator_1_lt));  // open: gt, eq
  Comparator #(.width(32)) comparator_2 (.a(A), .b(B), .gt(comparator_2_gt));  // open: eq, lt
  Comparator #(.mode("unsigned"), .width(32)) comparator_3 (.a(A), .b(B), .lt(comparator_3_lt));  // open: gt, eq
  Comparator #(.width(32)) comparator_4 (.a(A), .b(B), .gt(comparator_4_gt));  // open: eq, lt
  assign and_1_out = A & B;  // AND_Gate and_1, 32 bits wide
  assign or_1_out = A | B;  // OR_Gate or_1, 32 bits wide
  Adder #(.width(32)) adder_1 (.a(A), .b(B), .out(adder_1_out));  // open: cin, cout
  assign xor_1_out = A ^ B;  // XOR_Gate xor_1, 32 bits wide
  // extensorSinal_1 extensorsinal_1_1: pin names not known; wires that end beside it: comparator_1_lt, extensorsinal_1_1_p2
  Shifter #(.shift("ar"), .width(32)) shifter_1 (.in(A), .\dist (B[4:0]), .out(shifter_1_out));
  Subtractor #(.width(32)) subtractor_1 (.a(A), .b(B), .out(subtractor_1_out));  // open: bin, bout
  Shifter #(.width(32)) shifter_2 (.in(A), .\dist (B[4:0]), .out(shifter_2_out));
  Shifter #(.shift("lr"), .width(32)) shifter_3 (.in(A), .\dist (B[4:0]), .out(shifter_3_out));
  // extensorSinal_1 extensorsinal_1_2: pin names not known; wires that end beside it: comparator_2_gt, extensorsinal_1_2_p2
  // extensorSinal_1 extensorsinal_1_3: pin names not known; wires that end beside it: comparator_3_lt, extensorsinal_1_3_p2
  // extensorSinal_1 extensorsinal_1_4: pin names not known; wires that end beside it: comparator_4_gt, extensorsinal_1_4_p2
  Multiplexer #(.select(4), .width(32)) multiplexer_1 (
    .in0(and_1_out), .in1(or_1_out), .in2(adder_1_out), .in3(xor_1_out), .in4(extensorsinal_1_1_p2),
    .in5(shifter_1_out), .in6(subtractor_1_out), .in7(shifter_2_out), .in8(shifter_3_out),
    .in9(extensorsinal_1_2_p2), .in10(extensorsinal_1_3_p2), .in11(extensorsinal_1_4_p2), .in12({32{1'b0}}),
    .in13({32{1'b0}}), .in14({32{1'b0}}), .in15({32{1'b0}}), .out(Result), .sel(ALUControl));
  zero zero_1 (.Result(Result), .ZERO(sZero));

  // Other names for the same wires on the sheet: Shift[4:0] = B[4:0]

  // Notes on the sheet:
  //   Arithmetic
  //   Left
  //   Right
  //   Unsigned
  //   Unsigned
  //   Não usada
  //   Não usada
endmodule
