// Logisim project main.circ as structural Verilog: 1 circuit, main circuit main
module main (
);

  wire and_1_out, and_2_out, and_3_out, BranchSrc, CLK, estagioex_mem_1_jump_mem,
       estagioex_mem_1_memread_mem, estagioex_mem_1_memtoreg_mem, estagioex_mem_1_memwrite_mem,
       estagioex_mem_1_regwrite_mem, estagioid_ex_1_p22, estagioid_ex_1_p26, estagioid_ex_1_p27,
       estagioid_ex_1_p28, estagioid_ex_1_p29, estagioid_ex_1_p30, estagioid_ex_1_p31, estagioid_ex_1_p32,
       estagioid_ex_1_p33, estagioid_ex_1_p34, estagioid_ex_1_p35, estagioid_ex_1_p38, estagioid_ex_1_p41,
       estagioif_id_1_p5, estagioif_id_1_p8, estagiomem_wb_1_jump_wb, estagiomem_wb_1_memtoreg_wb,
       estagiomem_wb_1_regwrite_wb, Stop, ucenderecamento_1_signal_unsigned, ucprincipal_1_alusrcb,
       ucprincipal_1_auipc_uc, ucprincipal_1_branch, ucprincipal_1_jump, ucprincipal_1_lui_uc,
       ucprincipal_1_memread, ucprincipal_1_memtoreg, ucprincipal_1_memwrite, ucprincipal_1_pcsrc,
       ucprincipal_1_regwrite, ucula_1_p5, ucula_1_p6, ucula_1_p7, Zero;
  wire [1:0] ucenderecamento_1_offset, ucenderecamento_1_size, ucprincipal_1_aluop;
  wire [2:0] decodificador_1_funct3, estagioex_mem_1_f3_mem, estagioid_ex_1_p40;
  wire [3:0] ucenderecamento_1_byteenable;
  wire [4:0] decodificador_1_rd, decodificador_1_rs1, decodificador_1_rs2, estagioex_mem_1_rd_mem,
       estagioid_ex_1_p39, estagiomem_wb_1_rd_wb;
  wire [6:0] decodificador_1_funct7, decodificador_1_opcode;
  wire [31:0] adder_1_out, adder_2_out, ALU, bancoregistradores_1_ld1, bancoregistradores_1_ld2,
       contadorciclos_1_contador, decodificador_1_imm, estagioex_mem_1_aluresult_mem,
       estagioex_mem_1_ld2_mem, estagioex_mem_1_pcplus4_mem, estagioid_ex_1_p24, estagioid_ex_1_p25,
       estagioid_ex_1_p36, estagioid_ex_1_p37, estagioid_ex_1_p42, estagioif_id_1_p7,
       estagiomem_wb_1_aluresult_wb, estagiomem_wb_1_memdata_wb, estagiomem_wb_1_pcplus4_wb, Imm,
       Instrucao_EX, Instrucao_ID, Instrucao_IF, Instrucao_MEM, Instrucao_WB, LD1, LD2,
       memdados_1_dados_lidos, multiplexer_1_out, multiplexer_2_out, multiplexer_3_out, multiplexer_4_out,
       multiplexer_5_out, multiplexer_6_out, multiplexer_7_out, PC, PC_q, ula_1_p6;

  Multiplexer #(.width(32)) multiplexer_1 (
    .in0(adder_1_out), .in1(adder_2_out), .out(multiplexer_1_out), .sel(ucprincipal_1_pcsrc));
  // Probe on Imm
  and and_1 (and_1_out, CLK, ~Stop);  // AND_Gate
  // Probe on Instrucao_IF
  // Probe on contadorciclos_1_contador
  contadorCiclos contadorciclos_1 (.Clock(and_1_out), .Contador(contadorciclos_1_contador));
  Clock clock_1 (.out(CLK));
  Register #(.width(32)) u_PC (.D(multiplexer_2_out), .en(and_2_out), .clk(and_2_out), .Q(PC_q));  // open: clr
  Multiplexer #(.width(32)) multiplexer_2 (
    .in0(multiplexer_1_out), .in1(ula_1_p6), .out(multiplexer_2_out), .sel(estagioid_ex_1_p35));
  and and_2 (and_2_out, CLK, ~Stop);  // AND_Gate
  // Probe on PC
  // Probe on LD1
  // Probe on LD2
  // Probe on ALU
  Adder #(.width(32)) adder_1 (.a(32'h4), .b(PC_q), .out(adder_1_out));  // open: cin, cout
  memInstr meminstr_1 (.PC_address(PC_q), .Instruction(Instrucao_IF));
  // estagioIF_ID estagioif_id_1: pin names not known; wires that end beside it: adder_1_out, Instrucao_IF, PC_q, CLK, estagioif_id_1_p5, estagioif_id_1_p5, estagioif_id_1_p7, estagioif_id_1_p8, Instrucao_ID
  decodificador decodificador_1 (
    .instrucao(Instrucao_ID), .imm(decodificador_1_imm), .opcode(decodificador_1_opcode),
    .rd(decodificador_1_rd), .funct3(decodificador_1_funct3), .rs1(decodificador_1_rs1),
    .rs2(decodificador_1_rs2), .funct7(decodificador_1_funct7));
  ucPrincipal ucprincipal_1 (
    .BranchSrc(BranchSrc), .opcode(decodificador_1_opcode), .MemRead(ucprincipal_1_memread),
    .MemWrite(ucprincipal_1_memwrite), .Jump(ucprincipal_1_jump), .Branch(ucprincipal_1_branch),
    .S_Jalr(Stop), .RegWrite(ucprincipal_1_regwrite), .ALUOp(ucprincipal_1_aluop),
    .Auipc_uc(ucprincipal_1_auipc_uc), .ALUSrcB(ucprincipal_1_alusrcb), .Lui_uc(ucprincipal_1_lui_uc),
    .MemToReg(ucprincipal_1_memtoreg), .PCSrc(ucprincipal_1_pcsrc));  // open: Stop
  // Probe on Instrucao_ID
  bancoRegistradores bancoregistradores_1 (
    .RegWrite(estagiomem_wb_1_regwrite_wb), .LR1(decodificador_1_rs1), .LR2(decodificador_1_rs2),
    .WD(multiplexer_7_out), .WR(estagiomem_wb_1_rd_wb), .clk(CLK), .LD2(bancoregistradores_1_ld2),
    .LD1(bancoregistradores_1_ld1));
  ucDesvio ucdesvio_1 (.Zero(Zero), .funct3(decodificador_1_funct3), .BranchSrc(BranchSrc));
  idULA idula_1 (
    .A(bancoregistradores_1_ld1), .B(bancoregistradores_1_ld2), .funct3(decodificador_1_funct3), .Zero(Zero));
  Adder #(.width(32)) adder_2 (.a(estagioif_id_1_p7), .b(decodificador_1_imm), .out(adder_2_out));  // open: cin, cout
  // estagioID_EX estagioid_ex_1: pin names not known; wires that end beside it: estagioif_id_1_p7, estagioif_id_1_p8, ucprincipal_1_auipc_uc, ucprincipal_1_lui_uc, ucprincipal_1_jump, ucprincipal_1_aluop, ucprincipal_1_regwrite, ucprincipal_1_alusrcb, ucprincipal_1_memtoreg, ucprincipal_1_memread, ucprincipal_1_memwrite, ucprincipal_1_branch, bancoregistradores_1_ld1, bancoregistradores_1_ld2, decodificador_1_opcode, decodificador_1_rd, decodificador_1_funct3, decodificador_1_funct7, decodificador_1_imm, Instrucao_ID, CLK, estagioid_ex_1_p22, estagioid_ex_1_p22, estagioid_ex_1_p24, estagioid_ex_1_p25, estagioid_ex_1_p26, estagioid_ex_1_p27, estagioid_ex_1_p28, estagioid_ex_1_p29, estagioid_ex_1_p30, estagioid_ex_1_p31, estagioid_ex_1_p32, estagioid_ex_1_p33, estagioid_ex_1_p34, estagioid_ex_1_p35, estagioid_ex_1_p36, estagioid_ex_1_p37, estagioid_ex_1_p38, estagioid_ex_1_p39, estagioid_ex_1_p40, estagioid_ex_1_p41, estagioid_ex_1_p42, Instrucao_EX
  Multiplexer #(.width(32)) multiplexer_3 (
    .in0(estagioid_ex_1_p36), .in1(estagioid_ex_1_p24), .out(multiplexer_3_out), .sel(estagioid_ex_1_p26));
  Multiplexer #(.width(32)) multiplexer_4 (
    .in0(estagioid_ex_1_p37), .in1(estagioid_ex_1_p42), .out(multiplexer_4_out), .sel(estagioid_ex_1_p31));
  // ucULA ucula_1: pin names not known; wires that end beside it: estagioid_ex_1_p40, estagioid_ex_1_p41, estagioid_ex_1_p38, estagioid_ex_1_p29, ucula_1_p5, ucula_1_p6, ucula_1_p7
  // Probe on Instrucao_EX
  Multiplexer #(.width(32)) multiplexer_5 (
    .in0(multiplexer_3_out), .in1({32{1'b0}}), .out(multiplexer_5_out), .sel(estagioid_ex_1_p27));
  // ULA ula_1: pin names not known; wires that end beside it: multiplexer_5_out, multiplexer_4_out, ucula_1_p5, ucula_1_p6, ucula_1_p7, ula_1_p6
  estagioEX_MEM estagioex_mem_1 (
    .MemRead_EX(estagioid_ex_1_p33), .MemWrite_EX(estagioid_ex_1_p34), .CLK(CLK),
    .RegWrite_EX(estagioid_ex_1_p30), .MemToReg_EX(estagioid_ex_1_p32), .Jump_EX(estagioid_ex_1_p28),
    .Instrucao_EX(Instrucao_EX), .ALUResult_EX(ula_1_p6), .ld2_EX(estagioid_ex_1_p37),
    .rd_EX(estagioid_ex_1_p39), .PCplus4_EX(estagioid_ex_1_p25), .f3_EX(estagioid_ex_1_p40),
    .MemRead_MEM(estagioex_mem_1_memread_mem), .MemWrite_MEM(estagioex_mem_1_memwrite_mem),
    .RegWrite_MEM(estagioex_mem_1_regwrite_mem), .MemToReg_MEM(estagioex_mem_1_memtoreg_mem),
    .Jump_MEM(estagioex_mem_1_jump_mem), .Instrucao_MEM(Instrucao_MEM),
    .ALUResult_MEM(estagioex_mem_1_aluresult_mem), .ld2_MEM(estagioex_mem_1_ld2_mem),
    .rd_MEM(estagioex_mem_1_rd_mem), .PCplus4_MEM(estagioex_mem_1_pcplus4_mem),
    .f3_MEM(estagioex_mem_1_f3_mem));
  ucEnderecamento ucenderecamento_1 (
    .Adress(estagioex_mem_1_aluresult_mem), .Funct3(estagioex_mem_1_f3_mem),
    .writeEnable(estagioex_mem_1_memwrite_mem), .byteEnable(ucenderecamento_1_byteenable),
    .Size(ucenderecamento_1_size), .Offset(ucenderecamento_1_offset),
    .signal_unsigned(ucenderecamento_1_signal_unsigned));
  // Probe on Instrucao_MEM
  memDados memdados_1 (
    .Endereco(estagioex_mem_1_aluresult_mem), .clk(and_3_out), .MemRead(estagioex_mem_1_memread_mem),
    .byteEnable(ucenderecamento_1_byteenable), .dado(estagioex_mem_1_ld2_mem), .size(ucenderecamento_1_size),
    .offset(ucenderecamento_1_offset), .sUnsigned(ucenderecamento_1_signal_unsigned),
    .Dados_lidos(memdados_1_dados_lidos));
  and and_3 (and_3_out, CLK, ~Stop);  // AND_Gate
  estagioMEM_WB estagiomem_wb_1 (
    .RegWrite_MEM(estagioex_mem_1_regwrite_mem), .MemToReg_MEM(estagioex_mem_1_memtoreg_mem),
    .Jump_MEM(estagioex_mem_1_jump_mem), .CLK(CLK), .MemData_MEM(memdados_1_dados_lidos),
    .ALUResult_MEM(estagioex_mem_1_aluresult_mem), .rd_MEM(estagioex_mem_1_rd_mem),
    .PCplus4_MEM(estagioex_mem_1_pcplus4_mem), .Instrucao_MEM(Instrucao_MEM),
    .RegWrite_WB(estagiomem_wb_1_regwrite_wb), .MemToReg_WB(estagiomem_wb_1_memtoreg_wb),
    .Jump_WB(estagiomem_wb_1_jump_wb), .MemData_WB(estagiomem_wb_1_memdata_wb),
    .ALUResult_WB(estagiomem_wb_1_aluresult_wb), .rd_WB(estagiomem_wb_1_rd_wb),
    .PCplus4_WB(estagiomem_wb_1_pcplus4_wb), .Instrucao_WB(Instrucao_WB));
  // Probe on Instrucao_WB
  Multiplexer #(.width(32)) multiplexer_6 (
    .in0(estagiomem_wb_1_aluresult_wb), .in1(estagiomem_wb_1_memdata_wb), .out(multiplexer_6_out),
    .sel(estagiomem_wb_1_memtoreg_wb));
  Multiplexer #(.width(32)) multiplexer_7 (
    .in0(multiplexer_6_out), .in1(estagiomem_wb_1_pcplus4_wb), .out(multiplexer_7_out),
    .sel(estagiomem_wb_1_jump_wb));

  // Notes on the sheet:
  //   PC + 4
  //   PC + Imm
  //   PCSrc
  //   Jalr
  //   ALU_EX
  //   PC
  //   PC + 4
  //   AUIPC
  //   LUI
  //   Jump
  //   AluOP
  //   regWrite
  //   ALUSrc_B
  //   memToReg
  //   memRead
  //   memWrite
  //   ID1_EX
  //   ID2_EX
  //   OP
  //   rd
  //   f3
  //   f7
  //   IMM
  //   Instr
  //   Pc+4
  //   Jump
  //   regWrite
  //   ID2
  //   ALU
  //   f3
  //   RD
  //   Instr
  //   memToReg
  //   memRead
  //   memWrite
  //   Pc+4
  //   Jump
  //   ALU
  //   LD
  //   RD
  //   Instr
  //   memToReg
endmodule
