// Logisim project main.circ as structural Verilog: 1 circuit, main circuit main
module main (
);

  wire and_1_out, and_3_out, CLK, control_unit_1_alusrcb, control_unit_1_auipc_uc, control_unit_1_jump,
       control_unit_1_lui_uc, control_unit_1_memread, control_unit_1_memtoreg, control_unit_1_memwrite,
       control_unit_1_pcsrc, control_unit_1_read_rs1, control_unit_1_read_rs2, control_unit_1_regwrite,
       control_unit_1_s_jalr, estagioex_mem_1_jump_mem, estagioex_mem_1_memread_mem,
       estagioex_mem_1_memtoreg_mem, estagioex_mem_1_memwrite_mem, estagioif_id_1_p5, estagioif_id_1_p7,
       estagioif_id_1_p9, estagiomem_wb_1_jump_wb, estagiomem_wb_1_memtoreg_wb, Flush_IF,
       hazard_detection_unit_1_bubble_id, hazard_detection_unit_1_redirect_id, id_ex_stage_1_p21,
       id_ex_stage_1_p27, id_ex_stage_1_p28, id_ex_stage_1_p29, id_ex_stage_1_p30, id_ex_stage_1_p32,
       id_ex_stage_1_p33, id_ex_stage_1_p34, id_ex_stage_1_p35, id_ex_stage_1_p39, id_ex_stage_1_p42,
       idula_1_zero, Jalr_EX, or_1_out, or_2_out, RW_EX, RW_MEM, RW_WB, Stall, Stop, ucdesvio_1_branchsrc,
       ucenderecamento_1_signal_unsigned, ucula_1_p5, ucula_1_p6, ucula_1_p7;
  wire [1:0] control_unit_1_aluop, ucenderecamento_1_offset, ucenderecamento_1_size;
  wire [2:0] decodificador_1_funct3, estagioex_mem_1_f3_mem, id_ex_stage_1_p41;
  wire [3:0] ucenderecamento_1_byteenable;
  wire [4:0] decodificador_1_rd, decodificador_1_rs1, decodificador_1_rs2, rd_EX, rd_MEM, rd_WB;
  wire [6:0] decodificador_1_funct7, decodificador_1_opcode;
  wire [31:0] adder_1_out, adder_2_out, ALU, and_2_out, bancoregistradores_1_ld1, bancoregistradores_1_ld2,
       contadorciclos_1_contador, decodificador_1_imm, estagioex_mem_1_aluresult_mem,
       estagioex_mem_1_ld2_mem, estagioex_mem_1_pcplus4_mem, estagioif_id_1_p8, estagioif_id_1_p10,
       estagiomem_wb_1_aluresult_wb, estagiomem_wb_1_memdata_wb, estagiomem_wb_1_pcplus4_wb,
       id_ex_stage_1_p25, id_ex_stage_1_p26, id_ex_stage_1_p37, id_ex_stage_1_p38, id_ex_stage_1_p43, Imm,
       LD1, LD2, memdados_1_dados_lidos, meminstr_1_instruction, multiplexer_1_out, multiplexer_2_out,
       multiplexer_3_out, multiplexer_4_out, multiplexer_5_out, multiplexer_6_out, multiplexer_7_out,
       multiplexer_8_out, PC, PC_q, ula_1_p6;

  Multiplexer #(.width(32)) multiplexer_1 (
    .in0(adder_1_out), .in1(adder_2_out), .out(multiplexer_1_out), .sel(hazard_detection_unit_1_redirect_id));
  Multiplexer #(.width(32)) multiplexer_2 (
    .in0(multiplexer_1_out), .in1(and_2_out), .out(multiplexer_2_out), .sel(Jalr_EX));
  // Probe on Imm
  and and_1 (and_1_out, CLK, ~Stop);  // AND_Gate
  or or_1 (or_1_out, Jalr_EX, ~Stall);  // OR_Gate
  or or_2 (or_2_out, CLK, Stop);
  // Probe on contadorciclos_1_contador
  contadorCiclos contadorciclos_1 (.Clock(and_1_out), .Contador(contadorciclos_1_contador));
  Clock clock_1 (.out(CLK));
  Register #(.trigger("falling"), .width(32)) u_PC (
    .D(multiplexer_2_out), .en(or_1_out), .clk(or_2_out), .Q(PC_q));  // open: clr
  // Probe on PC
  // Probe on LD1
  // Probe on LD2
  // Probe on ALU
  memInstr meminstr_1 (.PC_address(PC_q), .Instruction(meminstr_1_instruction));
  Adder #(.width(32)) adder_1 (.a(32'h4), .b(PC_q), .out(adder_1_out));  // open: cin, cout
  // Probe on meminstr_1_instruction
  Multiplexer #(.width(32)) multiplexer_3 (
    .in0(meminstr_1_instruction), .in1(32'h13), .out(multiplexer_3_out), .sel(Flush_IF));
  // estagioIF_ID estagioif_id_1: pin names not known; wires that end beside it: adder_1_out, multiplexer_3_out, PC_q, CLK, estagioif_id_1_p5, estagioif_id_1_p5, estagioif_id_1_p7, estagioif_id_1_p8, estagioif_id_1_p9, estagioif_id_1_p10
  // Probe on estagioif_id_1_p10
  decodificador decodificador_1 (
    .instrucao(estagioif_id_1_p10), .imm(decodificador_1_imm), .opcode(decodificador_1_opcode),
    .rd(decodificador_1_rd), .funct3(decodificador_1_funct3), .rs1(decodificador_1_rs1),
    .rs2(decodificador_1_rs2), .funct7(decodificador_1_funct7));
  or or_3 (estagioif_id_1_p7, Jalr_EX, ~Stall);  // OR_Gate
  hazard_detection_unit hazard_detection_unit_1 (
    .Jalr_EX(Jalr_EX), .PCSrc_ID(control_unit_1_pcsrc), .rs1_ID(decodificador_1_rs1),
    .rs2_ID(decodificador_1_rs2), .rd_EX(rd_EX), .rd_MEM(rd_MEM), .read_rs1(control_unit_1_read_rs1),
    .read_rs2(control_unit_1_read_rs2), .RegWrite_EX(RW_EX), .RegWrite_MEM(RW_MEM), .Stall(Stall),
    .Flush_IF(Flush_IF), .Redirect_ID(hazard_detection_unit_1_redirect_id),
    .Bubble_ID(hazard_detection_unit_1_bubble_id));
  // Probe on decodificador_1_rs1
  // Probe on decodificador_1_rs2
  // Probe on rd_WB
  bancoRegistradores bancoregistradores_1 (
    .RegWrite(RW_WB), .LR1(decodificador_1_rs1), .LR2(decodificador_1_rs2), .WD(multiplexer_8_out),
    .WR(rd_WB), .clk(CLK), .LD2(bancoregistradores_1_ld2), .LD1(bancoregistradores_1_ld1));
  ucDesvio ucdesvio_1 (.Zero(idula_1_zero), .funct3(decodificador_1_funct3), .BranchSrc(ucdesvio_1_branchsrc));
  control_unit control_unit_1 (
    .BranchSrc(ucdesvio_1_branchsrc), .opcode(decodificador_1_opcode), .MemRead(control_unit_1_memread),
    .MemWrite(control_unit_1_memwrite), .Jump(control_unit_1_jump), .S_Jalr(control_unit_1_s_jalr),
    .read_rs2(control_unit_1_read_rs2), .read_rs1(control_unit_1_read_rs1),
    .RegWrite(control_unit_1_regwrite), .ALUOp(control_unit_1_aluop), .Auipc_uc(control_unit_1_auipc_uc),
    .ALUSrcB(control_unit_1_alusrcb), .Lui_uc(control_unit_1_lui_uc), .Stop(Stop),
    .MemToReg(control_unit_1_memtoreg), .PCSrc(control_unit_1_pcsrc));  // open: Branch
  idULA idula_1 (
    .A(bancoregistradores_1_ld1), .B(bancoregistradores_1_ld2), .funct3(decodificador_1_funct3),
    .Zero(idula_1_zero));
  // Probe on estagioif_id_1_p8
  // Probe on decodificador_1_imm
  // Probe on adder_2_out
  Adder #(.width(32)) adder_2 (.a(estagioif_id_1_p8), .b(decodificador_1_imm), .out(adder_2_out));  // open: cin, cout
  // ID_EX_stage id_ex_stage_1: pin names not known; wires that end beside it: estagioif_id_1_p8, estagioif_id_1_p9, control_unit_1_auipc_uc, control_unit_1_lui_uc, control_unit_1_jump, control_unit_1_aluop, control_unit_1_regwrite, control_unit_1_alusrcb, control_unit_1_memtoreg, control_unit_1_memread, control_unit_1_memwrite, control_unit_1_s_jalr, bancoregistradores_1_ld1, bancoregistradores_1_ld2, decodificador_1_opcode, decodificador_1_rd, decodificador_1_funct3, decodificador_1_funct7, decodificador_1_imm, CLK, id_ex_stage_1_p21, id_ex_stage_1_p21, hazard_detection_unit_1_bubble_id, 1'b1, id_ex_stage_1_p25, id_ex_stage_1_p26, id_ex_stage_1_p27, id_ex_stage_1_p28, id_ex_stage_1_p29, id_ex_stage_1_p30, RW_EX, id_ex_stage_1_p32, id_ex_stage_1_p33, id_ex_stage_1_p34, id_ex_stage_1_p35, Jalr_EX, id_ex_stage_1_p37, id_ex_stage_1_p38, id_ex_stage_1_p39, rd_EX, id_ex_stage_1_p41, id_ex_stage_1_p42, id_ex_stage_1_p43
  Multiplexer #(.width(32)) multiplexer_4 (
    .in0(id_ex_stage_1_p37), .in1(id_ex_stage_1_p25), .out(multiplexer_4_out), .sel(id_ex_stage_1_p27));
  Multiplexer #(.width(32)) multiplexer_5 (
    .in0(id_ex_stage_1_p38), .in1(id_ex_stage_1_p43), .out(multiplexer_5_out), .sel(id_ex_stage_1_p32));
  // ucULA ucula_1: pin names not known; wires that end beside it: id_ex_stage_1_p41, id_ex_stage_1_p42, id_ex_stage_1_p39, id_ex_stage_1_p30, ucula_1_p5, ucula_1_p6, ucula_1_p7
  // Probe on multiplexer_6_out
  Multiplexer #(.width(32)) multiplexer_6 (
    .in0(multiplexer_4_out), .in1({32{1'b0}}), .out(multiplexer_6_out), .sel(id_ex_stage_1_p28));
  // Probe on multiplexer_5_out
  // ULA ula_1: pin names not known; wires that end beside it: multiplexer_6_out, multiplexer_5_out, ucula_1_p5, ucula_1_p6, ucula_1_p7, ula_1_p6
  assign and_2_out = ula_1_p6 & 32'hfffffffe;  // AND_Gate and_2, 32 bits wide
  // Probe on ula_1_p6
  estagioEX_MEM estagioex_mem_1 (
    .MemRead_EX(id_ex_stage_1_p34), .MemWrite_EX(id_ex_stage_1_p35), .CLK(CLK), .RegWrite_EX(RW_EX),
    .MemToReg_EX(id_ex_stage_1_p33), .Jump_EX(id_ex_stage_1_p29), .ALUResult_EX(ula_1_p6),
    .ld2_EX(id_ex_stage_1_p38), .rd_EX(rd_EX), .PCplus4_EX(id_ex_stage_1_p26), .f3_EX(id_ex_stage_1_p41),
    .MemRead_MEM(estagioex_mem_1_memread_mem), .MemWrite_MEM(estagioex_mem_1_memwrite_mem),
    .RegWrite_MEM(RW_MEM), .MemToReg_MEM(estagioex_mem_1_memtoreg_mem), .Jump_MEM(estagioex_mem_1_jump_mem),
    .ALUResult_MEM(estagioex_mem_1_aluresult_mem), .ld2_MEM(estagioex_mem_1_ld2_mem), .rd_MEM(rd_MEM),
    .PCplus4_MEM(estagioex_mem_1_pcplus4_mem), .f3_MEM(estagioex_mem_1_f3_mem));  // open: Instrucao_EX, Instrucao_MEM
  ucEnderecamento ucenderecamento_1 (
    .Adress(estagioex_mem_1_aluresult_mem), .Funct3(estagioex_mem_1_f3_mem),
    .writeEnable(estagioex_mem_1_memwrite_mem), .byteEnable(ucenderecamento_1_byteenable),
    .Size(ucenderecamento_1_size), .Offset(ucenderecamento_1_offset),
    .signal_unsigned(ucenderecamento_1_signal_unsigned));
  memDados memdados_1 (
    .Endereco(estagioex_mem_1_aluresult_mem), .clk(and_3_out), .MemRead(estagioex_mem_1_memread_mem),
    .byteEnable(ucenderecamento_1_byteenable), .dado(estagioex_mem_1_ld2_mem), .size(ucenderecamento_1_size),
    .offset(ucenderecamento_1_offset), .sUnsigned(ucenderecamento_1_signal_unsigned),
    .Dados_lidos(memdados_1_dados_lidos));
  and and_3 (and_3_out, CLK, ~Stop);  // AND_Gate
  estagioMEM_WB estagiomem_wb_1 (
    .RegWrite_MEM(RW_MEM), .MemToReg_MEM(estagioex_mem_1_memtoreg_mem), .Jump_MEM(estagioex_mem_1_jump_mem),
    .CLK(CLK), .MemData_MEM(memdados_1_dados_lidos), .ALUResult_MEM(estagioex_mem_1_aluresult_mem),
    .rd_MEM(rd_MEM), .PCplus4_MEM(estagioex_mem_1_pcplus4_mem), .RegWrite_WB(RW_WB),
    .MemToReg_WB(estagiomem_wb_1_memtoreg_wb), .Jump_WB(estagiomem_wb_1_jump_wb),
    .MemData_WB(estagiomem_wb_1_memdata_wb), .ALUResult_WB(estagiomem_wb_1_aluresult_wb), .rd_WB(rd_WB),
    .PCplus4_WB(estagiomem_wb_1_pcplus4_wb));
  Multiplexer #(.width(32)) multiplexer_7 (
    .in0(estagiomem_wb_1_aluresult_wb), .in1(estagiomem_wb_1_memdata_wb), .out(multiplexer_7_out),
    .sel(estagiomem_wb_1_memtoreg_wb));
  Multiplexer #(.width(32)) multiplexer_8 (
    .in0(multiplexer_7_out), .in1(estagiomem_wb_1_pcplus4_wb), .out(multiplexer_8_out),
    .sel(estagiomem_wb_1_jump_wb));

  // Notes on the sheet:
  //   PCSrc
  //   PC + 4
  //   PC + Imm
  //   Jalr
  //   ALU_EX
  //   PC
  //   PC + 4
  //   AUIPC
  //   LUI
  //   Jump
  //   AluOP
  //   regWrite
  //   ALUSrc_B
  //   memToReg
  //   memRead
  //   memWrite
  //   ID1_EX
  //   ID2_EX
  //   OP
  //   rd
  //   f3
  //   f7
  //   IMM
  //   Pc+4
  //   Jump
  //   regWrite
  //   memToReg
  //   memRead
  //   memWrite
  //   ID2
  //   ALU
  //   f3
  //   RD
  //   Pc+4
  //   Jump
  //   memToReg
  //   ALU
  //   LD
  //   RD
endmodule
