// Logisim project bancoRegistradores.circ as structural Verilog: 1 circuit, main circuit bancoRegistradores
module bancoRegistradores (
  input  [4:0] LR1,
  input  [31:0] WD,
  input  [4:0] WR,
  input  [4:0] LR2,
  input  clk,
  input  RegWrite,
  output [31:0] LD1,
  output [31:0] LD2
);

  wire demultiplexer_2_out0, demultiplexer_2_out1, demultiplexer_2_out2, demultiplexer_2_out3,
       demultiplexer_2_out4, demultiplexer_2_out5, demultiplexer_2_out6, demultiplexer_2_out7,
       demultiplexer_2_out8, demultiplexer_2_out9, demultiplexer_2_out10, demultiplexer_2_out11,
       demultiplexer_2_out12, demultiplexer_2_out13, demultiplexer_2_out14, demultiplexer_2_out15,
       demultiplexer_2_out16, demultiplexer_2_out17, demultiplexer_2_out18, demultiplexer_2_out19,
       demultiplexer_2_out20, demultiplexer_2_out21, demultiplexer_2_out22, demultiplexer_2_out23,
       demultiplexer_2_out24, demultiplexer_2_out25, demultiplexer_2_out26, demultiplexer_2_out27,
       demultiplexer_2_out28, demultiplexer_2_out29, demultiplexer_2_out30, demultiplexer_2_out31;
  wire [31:0] _00_q, _01_q, _02_q, _03_q, _04_q, _05_q, _06_q, _07_q, _08_q, _09_q, _10_q, _11_q, _12_q,
       _13_q, _14_q, _15_q, _16_q, _17_q, _18_q, _19_q, _20_q, _21_q, _22_q, _23_q, _24_q, _25_q, _26_q,
       _27_q, _28_q, _29_q, _30_q, _31_q, demultiplexer_1_out0, demultiplexer_1_out1, demultiplexer_1_out2,
       demultiplexer_1_out3, demultiplexer_1_out4, demultiplexer_1_out5, demultiplexer_1_out6,
       demultiplexer_1_out7, demultiplexer_1_out8, demultiplexer_1_out9, demultiplexer_1_out10,
       demultiplexer_1_out11, demultiplexer_1_out12, demultiplexer_1_out13, demultiplexer_1_out14,
       demultiplexer_1_out15, demultiplexer_1_out16, demultiplexer_1_out17, demultiplexer_1_out18,
       demultiplexer_1_out19, demultiplexer_1_out20, demultiplexer_1_out21, demultiplexer_1_out22,
       demultiplexer_1_out23, demultiplexer_1_out24, demultiplexer_1_out25, demultiplexer_1_out26,
       demultiplexer_1_out27, demultiplexer_1_out28, demultiplexer_1_out29, demultiplexer_1_out30,
       demultiplexer_1_out31;

  // Probe on WD
  Demultiplexer #(.select(5), .width(32), .enable("false")) demultiplexer_1 (
    .out0(demultiplexer_1_out0), .out1(demultiplexer_1_out1), .out2(demultiplexer_1_out2),
    .out3(demultiplexer_1_out3), .out4(demultiplexer_1_out4), .out5(demultiplexer_1_out5),
    .out6(demultiplexer_1_out6), .out7(demultiplexer_1_out7), .out8(demultiplexer_1_out8),
    .out9(demultiplexer_1_out9), .out10(demultiplexer_1_out10), .out11(demultiplexer_1_out11),
    .out12(demultiplexer_1_out12), .out13(demultiplexer_1_out13), .out14(demultiplexer_1_out14),
    .out15(demultiplexer_1_out15), .out16(demultiplexer_1_out16), .out17(demultiplexer_1_out17),
    .out18(demultiplexer_1_out18), .out19(demultiplexer_1_out19), .out20(demultiplexer_1_out20),
    .out21(demultiplexer_1_out21), .out22(demultiplexer_1_out22), .out23(demultiplexer_1_out23),
    .out24(demultiplexer_1_out24), .out25(demultiplexer_1_out25), .out26(demultiplexer_1_out26),
    .out27(demultiplexer_1_out27), .out28(demultiplexer_1_out28), .out29(demultiplexer_1_out29),
    .out30(demultiplexer_1_out30), .out31(demultiplexer_1_out31), .in(WD), .sel(WR));
  Register #(.width(32)) _00 (.D(demultiplexer_1_out0), .Q(_00_q), .clk(clk), .clr(demultiplexer_2_out0));  // open: en
  Register #(.width(32)) _01 (.D(demultiplexer_1_out1), .en(demultiplexer_2_out1), .Q(_01_q), .clk(clk));  // open: clr
  Register #(.width(32)) _02 (.D(demultiplexer_1_out2), .en(demultiplexer_2_out2), .Q(_02_q), .clk(clk));  // open: clr
  Register #(.width(32)) _03 (.D(demultiplexer_1_out3), .en(demultiplexer_2_out3), .Q(_03_q), .clk(clk));  // open: clr
  Register #(.width(32)) _04 (.D(demultiplexer_1_out4), .en(demultiplexer_2_out4), .Q(_04_q), .clk(clk));  // open: clr
  Register #(.width(32)) _05 (.D(demultiplexer_1_out5), .en(demultiplexer_2_out5), .Q(_05_q), .clk(clk));  // open: clr
  Register #(.width(32)) _06 (.D(demultiplexer_1_out6), .en(demultiplexer_2_out6), .Q(_06_q), .clk(clk));  // open: clr
  Register #(.width(32)) _07 (.D(demultiplexer_1_out7), .en(demultiplexer_2_out7), .Q(_07_q), .clk(clk));  // open: clr
  Register #(.width(32)) _08 (.D(demultiplexer_1_out8), .en(demultiplexer_2_out8), .Q(_08_q), .clk(clk));  // open: clr
  Register #(.width(32)) _09 (.D(demultiplexer_1_out9), .en(demultiplexer_2_out9), .Q(_09_q), .clk(clk));  // open: clr
  Register #(.width(32)) _10 (
    .D(demultiplexer_1_out10), .en(demultiplexer_2_out10), .Q(_10_q), .clk(clk));  // open: clr
  Register #(.width(32)) _11 (
    .D(demultiplexer_1_out11), .en(demultiplexer_2_out11), .Q(_11_q), .clk(clk));  // open: clr
  Register #(.width(32)) _12 (
    .D(demultiplexer_1_out12), .en(demultiplexer_2_out12), .Q(_12_q), .clk(clk));  // open: clr
  Register #(.width(32)) _13 (
    .D(demultiplexer_1_out13), .en(demultiplexer_2_out13), .Q(_13_q), .clk(clk));  // open: clr
  Register #(.width(32)) _14 (
    .D(demultiplexer_1_out14), .en(demultiplexer_2_out14), .Q(_14_q), .clk(clk));  // open: clr
  Register #(.width(32)) _15 (
    .D(demultiplexer_1_out15), .en(demultiplexer_2_out15), .Q(_15_q), .clk(clk));  // open: clr
  Register #(.width(32)) _16 (
    .D(demultiplexer_1_out16), .en(demultiplexer_2_out16), .Q(_16_q), .clk(clk));  // open: clr
  Register #(.width(32)) _17 (
    .D(demultiplexer_1_out17), .en(demultiplexer_2_out17), .Q(_17_q), .clk(clk));  // open: clr
  Register #(.width(32)) _18 (
    .D(demultiplexer_1_out18), .en(demultiplexer_2_out18), .Q(_18_q), .clk(clk));  // open: clr
  Register #(.width(32)) _19 (
    .D(demultiplexer_1_out19), .en(demultiplexer_2_out19), .Q(_19_q), .clk(clk));  // open: clr
  Register #(.width(32)) _20 (
    .D(demultiplexer_1_out20), .en(demultiplexer_2_out20), .Q(_20_q), .clk(clk));  // open: clr
  Register #(.width(32)) _21 (
    .D(demultiplexer_1_out21), .en(demultiplexer_2_out21), .Q(_21_q), .clk(clk));  // open: clr
  Register #(.width(32)) _22 (
    .D(demultiplexer_1_out22), .en(demultiplexer_2_out22), .Q(_22_q), .clk(clk));  // open: clr
  Register #(.width(32)) _23 (
    .D(demultiplexer_1_out23), .en(demultiplexer_2_out23), .Q(_23_q), .clk(clk));  // open: clr
  Register #(.width(32)) _24 (
    .D(demultiplexer_1_out24), .en(demultiplexer_2_out24), .Q(_24_q), .clk(clk));  // open: clr
  Register #(.width(32)) _25 (
    .D(demultiplexer_1_out25), .en(demultiplexer_2_out25), .Q(_25_q), .clk(clk));  // open: clr
  Register #(.width(32)) _26 (
    .D(demultiplexer_1_out26), .en(demultiplexer_2_out26), .Q(_26_q), .clk(clk));  // open: clr
  Register #(.width(32)) _27 (
    .D(demultiplexer_1_out27), .en(demultiplexer_2_out27), .Q(_27_q), .clk(clk));  // open: clr
  Register #(.width(32)) _28 (
    .D(demultiplexer_1_out28), .en(demultiplexer_2_out28), .Q(_28_q), .clk(clk));  // open: clr
  Register #(.width(32)) _29 (
    .D(demultiplexer_1_out29), .en(demultiplexer_2_out29), .Q(_29_q), .clk(clk));  // open: clr
  Register #(.width(32)) _30 (
    .D(demultiplexer_1_out30), .en(demultiplexer_2_out30), .Q(_30_q), .clk(clk));  // open: clr
  Register #(.width(32)) _31 (
    .D(demultiplexer_1_out31), .en(demultiplexer_2_out31), .Q(_31_q), .clk(clk));  // open: clr
  Demultiplexer #(.select(5), .enable("false")) demultiplexer_2 (
    .out0(demultiplexer_2_out0), .out1(demultiplexer_2_out1), .out2(demultiplexer_2_out2),
    .out3(demultiplexer_2_out3), .out4(demultiplexer_2_out4), .out5(demultiplexer_2_out5),
    .out6(demultiplexer_2_out6), .out7(demultiplexer_2_out7), .out8(demultiplexer_2_out8),
    .out9(demultiplexer_2_out9), .out10(demultiplexer_2_out10), .out11(demultiplexer_2_out11),
    .out12(demultiplexer_2_out12), .out13(demultiplexer_2_out13), .out14(demultiplexer_2_out14),
    .out15(demultiplexer_2_out15), .out16(demultiplexer_2_out16), .out17(demultiplexer_2_out17),
    .out18(demultiplexer_2_out18), .out19(demultiplexer_2_out19), .out20(demultiplexer_2_out20),
    .out21(demultiplexer_2_out21), .out22(demultiplexer_2_out22), .out23(demultiplexer_2_out23),
    .out24(demultiplexer_2_out24), .out25(demultiplexer_2_out25), .out26(demultiplexer_2_out26),
    .out27(demultiplexer_2_out27), .out28(demultiplexer_2_out28), .out29(demultiplexer_2_out29),
    .out30(demultiplexer_2_out30), .out31(demultiplexer_2_out31), .in(RegWrite), .sel(WR));
  Multiplexer #(.select(5), .width(32), .enable("false")) multiplexer_1 (
    .in0(_00_q), .in1(_01_q), .in2(_02_q), .in3(_03_q), .in4(_04_q), .in5(_05_q), .in6(_06_q), .in7(_07_q),
    .in8(_08_q), .in9(_09_q), .in10(_10_q), .in11(_11_q), .in12(_12_q), .in13(_13_q), .in14(_14_q),
    .in15(_15_q), .in16(_16_q), .in17(_17_q), .in18(_18_q), .in19(_19_q), .in20(_20_q), .in21(_21_q),
    .in22(_22_q), .in23(_23_q), .in24(_24_q), .in25(_25_q), .in26(_26_q), .in27(_27_q), .in28(_28_q),
    .in29(_29_q), .in30(_30_q), .in31(_31_q), .out(LD1), .sel(LR1));
  Multiplexer #(.select(5), .width(32), .enable("false")) multiplexer_2 (
    .in0(_00_q), .in1(_01_q), .in2(_02_q), .in3(_03_q), .in4(_04_q), .in5(_05_q), .in6(_06_q), .in7(_07_q),
    .in8(_08_q), .in9(_09_q), .in10(_10_q), .in11(_11_q), .in12(_12_q), .in13(_13_q), .in14(_14_q),
    .in15(_15_q), .in16(_16_q), .in17(_17_q), .in18(_18_q), .in19(_19_q), .in20(_20_q), .in21(_21_q),
    .in22(_22_q), .in23(_23_q), .in24(_24_q), .in25(_25_q), .in26(_26_q), .in27(_27_q), .in28(_28_q),
    .in29(_29_q), .in30(_30_q), .in31(_31_q), .out(LD2), .sel(LR2));
endmodule
