// Logisim project conc.circ as structural Verilog: 1 circuit, main circuit conc
module conc (
  input  [25:0] address,
  input  [31:0] pc_p4,
  output [31:0] jump_address
);


  assign jump_address = {pc_p4[31:28], {8{1'b0}}, address[17:0], 2'b00};

  // Other names for the same wires on the sheet: addr[25:0] = address
endmodule
