// Logisim project decodificador.circ as structural Verilog: 1 circuit, main circuit decodificador
module decodificador (
  input  [31:0] \instrução ,
  output [6:0] opcode,
  output [4:0] rd,
  output [2:0] funct3,
  output [4:0] rs1,
  output [4:0] rs2,
  output [6:0] funct7
);


  assign funct3 = \instrução [14:12];
  assign funct7 = \instrução [31:25];
  assign opcode = \instrução [6:0];
  assign rd = \instrução [11:7];
  assign rs1 = \instrução [19:15];
  assign rs2 = \instrução [24:20];
endmodule
