// Logisim project main.circ as structural Verilog: 1 circuit, main circuit main
module main (
);

  wire ALUSrcB, and_1_out, and_2_out, and_3_out, Branch, BranchSrc, CLK, Jalr, Jump, MemRead, MemToReg,
       MemWrite, Neg, PCSrc, RegWrite, Stop, Zero;
  wire [1:0] ALUOp, ALUSrcA;
  wire [2:0] decodificador_1_funct3, ImmSrc;
  wire [3:0] ucula_1_alucontrol;
  wire [4:0] decodificador_1_rd, decodificador_1_rs1, decodificador_1_rs2;
  wire [6:0] decodificador_1_funct7, decodificador_1_opcode;
  wire [31:0] adder_1_out, bancoregistradores_1_ld2, contador_1_contador, datamem_1_dados_lidos, Imm, LD1,
       LD2, meminstr_1_instruction, multiplexer_1_out, multiplexer_2_out, multiplexer_3_out,
       multiplexer_4_out, PC, PC_p4, ULA, WD;

  Adder #(.width(32)) adder_1 (.a(PC), .b(Imm), .out(adder_1_out));  // open: cin, cout
  and and_1 (and_1_out, CLK, ~Stop);  // AND_Gate
  Multiplexer #(.width(32), .enable("false")) multiplexer_1 (
    .in0(PC_p4), .in1(adder_1_out), .out(multiplexer_1_out), .sel(PCSrc));
  // Probe on Imm
  contador contador_1 (.Clock(and_1_out), .Contador(contador_1_contador));
  Clock clock_1 (.out(CLK));
  Multiplexer #(.width(32), .enable("false")) multiplexer_2 (
    .in0(multiplexer_1_out), .in1(ULA), .out(multiplexer_2_out), .sel(Jalr));
  // Probe on contador_1_contador
  Register #(.width(32)) u_PC (.D(multiplexer_2_out), .Q(PC), .clk(and_2_out));  // open: en, clr
  and and_2 (and_2_out, CLK, ~Stop);  // AND_Gate
  // Probe on PC
  // Probe on LD1
  // Probe on LD2
  // Probe on ULA
  Adder #(.width(32)) adder_2 (.a(32'h4), .b(PC), .out(PC_p4));  // open: cin, cout
  MemInstr meminstr_1 (.PC_address(PC), .Instruction(meminstr_1_instruction));
  decodificador decodificador_1 (
    .instrucao(meminstr_1_instruction), .opcode(decodificador_1_opcode), .rd(decodificador_1_rd),
    .funct3(decodificador_1_funct3), .rs1(decodificador_1_rs1), .rs2(decodificador_1_rs2),
    .funct7(decodificador_1_funct7));
  // Probe on decodificador_1_opcode
  immGen immgen_1 (.instrucao(meminstr_1_instruction), .ImmSrc(ImmSrc), .imm(Imm));
  // Probe on decodificador_1_rs1
  // Probe on decodificador_1_rs2
  ucBranch_main main_1 (.Zero(Zero), .Neg(Neg), .funct3(decodificador_1_funct3), .BranchSrc(BranchSrc));
  ucPrincipal ucprincipal_1 (
    .opcode(decodificador_1_opcode), .RegWrite(RegWrite), .ALUSrcB(ALUSrcB), .MemToReg(MemToReg),
    .MemRead(MemRead), .MemWrite(MemWrite), .PCSrc(PCSrc), .Branch(Branch), .ALUOp(ALUOp), .Jalr(Jalr),
    .Jump(Jump), .ImmSrc(ImmSrc), .Stop(Stop), .BranchSrc(BranchSrc), .AluSrcA(ALUSrcA));
  // Probe on decodificador_1_rd
  Multiplexer #(.width(32), .enable("false")) multiplexer_3 (
    .in0(WD), .in1(PC_p4), .out(multiplexer_3_out), .sel(Jump));
  ucULA ucula_1 (
    .funct7(decodificador_1_funct7), .funct3(decodificador_1_funct3), .ALUOp(ALUOp),
    .ALUControl(ucula_1_alucontrol));
  bancoRegistradores bancoregistradores_1 (
    .RegWrite(RegWrite), .LR1(decodificador_1_rs1), .LR2(decodificador_1_rs2), .WD(multiplexer_3_out),
    .WR(decodificador_1_rd), .clk(CLK), .LD2(bancoregistradores_1_ld2), .LD1(LD1));
  Multiplexer #(.select(2), .width(32), .enable("false")) multiplexer_4 (
    .in0(LD1), .in1({32{1'b0}}), .in2(PC), .out(multiplexer_4_out), .sel(ALUSrcA));  // open: in3
  Multiplexer #(.width(32), .enable("false")) multiplexer_5 (
    .in0(bancoregistradores_1_ld2), .in1(Imm), .out(LD2), .sel(ALUSrcB));
  ula ula_1 (.ZERO(Zero), .Result(ULA), .A(multiplexer_4_out), .B(LD2), .ALUControl(ucula_1_alucontrol), .NEG(Neg));
  datamem datamem_1 (
    .Escreve_dado(bancoregistradores_1_ld2), .Endereco(ULA), .MemWrite(MemWrite), .clk(and_3_out),
    .MemRead(MemRead), .Dados_lidos(datamem_1_dados_lidos));  // open: clear
  and and_3 (and_3_out, CLK, ~Stop);  // AND_Gate
  Multiplexer #(.width(32), .enable("false")) multiplexer_6 (
    .in0(ULA), .in1(datamem_1_dados_lidos), .out(WD), .sel(MemToReg));

  // Notes on the sheet:
  //   TypeB_Jal
  //   rs1_Imm
  //   Opcode
  //   rs2
  //   rs1
  //   rd
  //   Mux jump
  //   rs2
  //   Imm
  //   Mux rd
endmodule
