// Logisim project memdados.circ as structural Verilog: 1 circuit, main circuit datamem
module datamem (
  input  [31:0] Endereco,
  input  clk,
  input  MemRead,
  input  [3:0] byteEnable,
  input  [31:0] dado,
  input  [1:0] size,
  input  [1:0] offset,
  input  sUnsigned,
  output [31:0] Dados_lidos
);

  wire [1:0] size_t;
  wire [7:0] multiplexer_2_out, ram_1_dout, ram_2_dout, ram_3_dout;
  wire [15:0] multiplexer_3_out;
  wire [31:0] bit_extender_1_out, bit_extender_2_out, bit_extender_3_out, multiplexer_1_out,
       multiplexer_4_out;
  wire [31:24] banco0_dout;

  Multiplexer #(.select(2), .width(32)) multiplexer_1 (
    .in0(dado), .in1({dado[15:0], dado[15:0]}), .in2({dado[7:0], dado[7:0], dado[7:0], dado[7:0]}),
    .out(multiplexer_1_out), .sel(size));  // open: in3
  RAM #(.addrWidth(24), .trigger("falling")) banco0 (
    .addr(Endereco[25:2]), .we(byteEnable[0]), .oe(MemRead), .clk(clk), .din(multiplexer_1_out[7:0]),
    .dout(banco0_dout));
  Multiplexer #(.select(2), .width(8)) multiplexer_2 (
    .in0(banco0_dout), .in1(ram_1_dout), .in2(ram_2_dout), .in3(ram_3_dout), .out(multiplexer_2_out),
    .sel(Endereco[1:0]));
  Multiplexer #(.width(16)) multiplexer_3 (
    .in0({banco0_dout, ram_1_dout}), .in1({ram_2_dout, ram_3_dout}), .out(multiplexer_3_out),
    .sel(Endereco[1]));
  assign bit_extender_1_out = {{24{multiplexer_2_out[7]}}, multiplexer_2_out};  // Bit_Extender bit_extender_1
  RAM #(.addrWidth(24), .trigger("falling")) ram_1 (
    .addr(Endereco[25:2]), .we(byteEnable[1]), .oe(MemRead), .clk(clk), .din(multiplexer_1_out[15:8]),
    .dout(ram_1_dout));
  assign bit_extender_2_out = {{16{multiplexer_3_out[15]}}, multiplexer_3_out};  // Bit_Extender bit_extender_2
  assign bit_extender_3_out = {{16{1'b0}}, multiplexer_3_out};  // Bit_Extender bit_extender_3
  Multiplexer #(.width(32)) multiplexer_4 (
    .in0(bit_extender_2_out), .in1(bit_extender_3_out), .out(multiplexer_4_out), .sel(sUnsigned));
  Multiplexer #(.select(2), .width(32)) multiplexer_5 (
    .in0(multiplexer_4_out), .in1(bit_extender_1_out),
    .in2({banco0_dout, ram_1_dout, ram_2_dout, ram_3_dout}), .out(Dados_lidos), .sel(size_t));  // open: in3
  RAM #(.addrWidth(24), .trigger("falling")) ram_2 (
    .addr(Endereco[25:2]), .we(byteEnable[2]), .oe(MemRead), .clk(clk), .din(multiplexer_1_out[23:16]),
    .dout(ram_2_dout));
  RAM #(.addrWidth(24), .trigger("falling")) ram_3 (
    .addr(Endereco[25:2]), .we(byteEnable[3]), .oe(MemRead), .clk(clk), .din(multiplexer_1_out[31:24]),
    .dout(ram_3_dout));

  assign offset = Endereco[1:0];
endmodule
