// Logisim project negativo.circ as structural Verilog: 1 circuit, main circuit negativo
module negativo (
  input  [31:0] ULA,
  output Negativo
);


  assign Negativo = ULA[31];
endmodule
