// Logisim project ucBranch.circ as structural Verilog: 1 circuit, main circuit main
module main (
  input  Zero,
  input  Neg,
  input  [2:0] funct3,
  output BranchSrc
);

  wire and_1_out, and_2_out, and_3_out, and_4_out, beq_out, bge_out, blt_out, bne_out;

  and beq (beq_out, ~funct3[2], ~funct3[1], ~funct3[0]);  // AND_Gate
  and and_1 (and_1_out, beq_out, Zero);
  and bne (bne_out, ~funct3[2], ~funct3[1], funct3[0]);  // AND_Gate
  and and_2 (and_2_out, bne_out, ~Zero);  // AND_Gate
  and blt (blt_out, funct3[2], ~funct3[1], ~funct3[0]);  // AND_Gate
  and and_3 (and_3_out, blt_out, Neg);
  or or_1 (BranchSrc, and_1_out, and_2_out, and_3_out, and_4_out);
  and bge (bge_out, funct3[2], ~funct3[1], funct3[0]);  // AND_Gate
  and and_4 (and_4_out, bge_out, ~Neg);  // AND_Gate
endmodule
