// Logisim project ucULA.circ as structural Verilog: 1 circuit, main circuit ucULA
module ucULA (
  input  [6:0] funct7,
  input  [1:0] ALUOp,
  input  [2:0] funct3,
  output [3:0] ALUControl,
  output Bne
);

  wire BGE, BLT, Seletor;
  wire [3:0] multiplexer_1_out, multiplexer_2_out, multiplexer_3_out, undriven, undriven_2, undriven_3;

  and and_1 (Seletor, funct7[5], ~funct7[4]);  // AND_Gate
  Multiplexer #(.width(4), .enable("false")) multiplexer_1 (
    .in0(4'b0010), .in1(4'b0110), .out(multiplexer_1_out), .sel(Seletor));
  Multiplexer #(.width(4), .enable("false")) multiplexer_2 (
    .in0(4'b1000), .in1(4'b0101), .out(multiplexer_2_out), .sel(funct7[5]));
  Multiplexer #(.select(3), .width(4), .enable("false")) multiplexer_3 (
    .in0(multiplexer_1_out), .in1(4'b0111), .in2(undriven), .in3(undriven_2), .in4(4'b0011),
    .in5(multiplexer_2_out), .in6(4'b0001), .in7(4'b0000), .out(multiplexer_3_out), .sel(funct3));
  and and_2 (Bne, funct3[0], ~funct3[1], ~funct3[2]);  // AND_Gate
  and and_3 (BLT, ~funct3[0], ~funct3[1], funct3[2]);  // AND_Gate
  and and_4 (BGE, funct3[0], ~funct3[1], funct3[2]);  // AND_Gate
  Multiplexer #(.select(2), .width(4), .enable("false")) multiplexer_4 (
    .in0(4'b0010), .in1(4'b0110), .in2(multiplexer_3_out), .in3(undriven_3), .out(ALUControl), .sel(ALUOp));

  // Notes on the sheet:
  //   add
  //   sub
  //   srl/srli
  //   sra/srai
  //   sll/slli
  //   xor/xori
  //   or/ori
  //   and/andi
  //   lw/sw
  //   B-type
  //   R-type/I-type
endmodule
