// Logisim project ula.circ as structural Verilog: 1 circuit, main circuit ula
module ula (
  input  [31:0] A,
  input  [31:0] B,
  input  [3:0] ALUControl,
  output NEG,
  output ZERO,
  output [31:0] Result,
  output Overflow
);

  wire comparator_1_lt, comparator_2_gt;
  wire [31:0] adder_1_out, and_1_out, bit_extender_1_out, bit_extender_2_out, or_1_out, shifter_1_out,
       shifter_2_out, shifter_3_out, subtractor_1_out, xor_1_out;

  // Probe on A
  // Probe on B
  Comparator #(.width(32)) comparator_1 (.a(A), .b(B), .lt(comparator_1_lt));  // open: gt, eq
  Comparator #(.width(32)) comparator_2 (.a(A), .b(B), .gt(comparator_2_gt));  // open: eq, lt
  assign and_1_out = A & B;  // AND_Gate and_1, 32 bits wide
  assign or_1_out = A | B;  // OR_Gate or_1, 32 bits wide
  Adder #(.width(32)) adder_1 (.a(A), .b(B), .out(adder_1_out));  // open: cin, cout
  assign xor_1_out = A ^ B;  // XOR_Gate xor_1, 32 bits wide
  assign bit_extender_1_out = {{31{1'b0}}, comparator_1_lt};  // Bit_Extender bit_extender_1
  Shifter #(.width(32), .shift("ar")) shifter_1 (.in(A), .\dist (B[4:0]), .out(shifter_1_out));
  Subtractor #(.width(32)) subtractor_1 (.a(A), .b(B), .out(subtractor_1_out));  // open: bin, bout
  Shifter #(.width(32)) shifter_2 (.in(A), .\dist (B[4:0]), .out(shifter_2_out));
  Shifter #(.width(32), .shift("lr")) shifter_3 (.in(A), .\dist (B[4:0]), .out(shifter_3_out));
  assign bit_extender_2_out = {{31{1'b0}}, comparator_2_gt};  // Bit_Extender bit_extender_2
  Multiplexer #(.select(4), .width(32), .enable("false")) multiplexer_1 (
    .in0(and_1_out), .in1(or_1_out), .in2(adder_1_out), .in3(xor_1_out), .in4(bit_extender_1_out),
    .in5(shifter_1_out), .in6(subtractor_1_out), .in7(shifter_2_out), .in8(shifter_3_out),
    .in9(bit_extender_2_out), .in10({32{1'b0}}), .in11({32{1'b0}}), .in12({32{1'b0}}), .in13({32{1'b0}}),
    .in14({32{1'b0}}), .in15({32{1'b0}}), .out(Result), .sel(ALUControl));
  negativo negativo_1 (.ULA(Result), .Negativo(NEG));
  zero zero_1 (.Result(Result), .ZERO(ZERO));
  overflow overflow_1 (.out_5(Overflow), .Operador(ALUControl), .a(A), .b(B), .Result(Result));

  // Other names for the same wires on the sheet: Shift[4:0] = B[4:0]
endmodule
