// Logisim project main.circ as structural Verilog: 1 circuit, main circuit main
module main (
);

  wire ALUSrcB, and_1_out, and_2_out, and_3_out, Auipc, Branch, BranchSrc, CLK, Jalr, Jump, LessU, Lui,
       MemRead, MemToReg, MemWrite, Neg, PCSrc, RegWrite, Stop, sUnsigned, Zero;
  wire [1:0] ALUOp, offset, ucenderecamento_1_size;
  wire [2:0] decodificador_1_funct3, ImmSrc;
  wire [3:0] ucenderecamento_1_byteenable, ucula_1_alucontrol;
  wire [4:0] decodificador_1_rd, decodificador_1_rs1, decodificador_1_rs2;
  wire [6:0] decodificador_1_funct7, decodificador_1_opcode;
  wire [31:0] adder_1_out, ALU, bancoregistradores_1_ld2, contador_1_contador, datamem_1_dados_lidos, Imm,
       LD1, LD2, meminstr_1_instruction, multiplexer_1_out, multiplexer_2_out, multiplexer_3_out,
       multiplexer_4_out, multiplexer_6_out, PC, PC_p4, WD;

  Adder #(.width(32)) adder_1 (.a(PC), .b(Imm), .out(adder_1_out));  // open: cin, cout
  Multiplexer #(.width(32)) multiplexer_1 (.in0(PC_p4), .in1(adder_1_out), .out(multiplexer_1_out), .sel(PCSrc));
  // Probe on Imm
  and and_1 (and_1_out, CLK, ~Stop);  // AND_Gate
  // Probe on contador_1_contador
  contador contador_1 (.Clock(and_1_out), .Contador(contador_1_contador));
  Clock clock_1 (.out(CLK));
  Register #(.width(32)) u_PC (.D(multiplexer_2_out), .clk(and_2_out), .Q(PC));  // open: en, clr
  Multiplexer #(.width(32)) multiplexer_2 (.in0(multiplexer_1_out), .in1(ALU), .out(multiplexer_2_out), .sel(Jalr));
  and and_2 (and_2_out, CLK, ~Stop);  // AND_Gate
  // Probe on PC
  // Probe on LD1
  // Probe on LD2
  // Probe on ALU
  Adder #(.width(32)) adder_2 (.a(32'h4), .b(PC), .out(PC_p4));  // open: cin, cout
  MemInstr meminstr_1 (.PC_address(PC), .Instruction(meminstr_1_instruction));
  // Probe on meminstr_1_instruction
  decodificador decodificador_1 (
    .\instrução (meminstr_1_instruction), .opcode(decodificador_1_opcode), .rd(decodificador_1_rd),
    .funct3(decodificador_1_funct3), .rs1(decodificador_1_rs1), .rs2(decodificador_1_rs2),
    .funct7(decodificador_1_funct7));
  // Probe on decodificador_1_opcode
  immGen immgen_1 (.instrucao(meminstr_1_instruction), .imm(Imm), .ImmSrc(ImmSrc));
  // Probe on decodificador_1_rs1
  // Probe on decodificador_1_rs2
  ucBranch_main main_1 (
    .Zero(Zero), .Neg(Neg), .LessUnsigned(LessU), .funct3(decodificador_1_funct3), .BranchSrc(BranchSrc));
  ucPrincipal ucprincipal_1 (
    .BranchSrc(BranchSrc), .opcode(decodificador_1_opcode), .MemRead(MemRead), .MemWrite(MemWrite),
    .Branch(Branch), .ImmSrc(ImmSrc), .out_14(Jalr), .Jump(Jump), .RegWrite(RegWrite), .ALUOp(ALUOp),
    .Auipc_uc(Auipc), .ALUSrcB(ALUSrcB), .Lui_uc(Lui), .Stop(Stop), .MemToReg(MemToReg), .PCSrc(PCSrc));
  // Probe on decodificador_1_rd
  Multiplexer #(.width(32)) multiplexer_3 (.in0(WD), .in1(PC_p4), .out(multiplexer_3_out), .sel(Jump));
  ucULA ucula_1 (
    .funct7(decodificador_1_funct7), .funct3(decodificador_1_funct3), .ALUOp(ALUOp),
    .ALUControl(ucula_1_alucontrol));
  bancoRegistradores bancoregistradores_1 (
    .WD(multiplexer_3_out), .WR(decodificador_1_rd), .LD1(LD1), .LR1(decodificador_1_rs1),
    .LD2(bancoregistradores_1_ld2), .LR2(decodificador_1_rs2), .clk(CLK), .RegWrite(RegWrite));
  ucEnderecamento ucenderecamento_1 (
    .Funct3(decodificador_1_funct3), .writeEnable(MemWrite), .Adress(ALU),
    .byteEnable(ucenderecamento_1_byteenable), .Size(ucenderecamento_1_size), .Offset(offset),
    .signal_unsigned(sUnsigned));
  Multiplexer #(.width(32)) multiplexer_4 (.in0(LD1), .in1(PC), .out(multiplexer_4_out), .sel(Auipc));
  Multiplexer #(.width(32)) multiplexer_5 (.in0(bancoregistradores_1_ld2), .in1(Imm), .out(LD2), .sel(ALUSrcB));
  Multiplexer #(.width(32)) multiplexer_6 (
    .in0(multiplexer_4_out), .in1({32{1'b0}}), .out(multiplexer_6_out), .sel(Lui));
  ULA ula_1 (
    .B(LD2), .ALUControl(ucula_1_alucontrol), .A(multiplexer_6_out), .sZero(Zero), .NEG(Neg), .Result(ALU),
    .LessUnsigned(LessU));
  datamem datamem_1 (
    .Endereco(ALU), .clk(and_3_out), .MemRead(MemRead), .byteEnable(ucenderecamento_1_byteenable),
    .dado(bancoregistradores_1_ld2), .size(ucenderecamento_1_size), .offset(offset), .sUnsigned(sUnsigned),
    .Dados_lidos(datamem_1_dados_lidos));
  and and_3 (and_3_out, CLK, ~Stop);  // AND_Gate
  Multiplexer #(.width(32)) multiplexer_7 (.in0(ALU), .in1(datamem_1_dados_lidos), .out(WD), .sel(MemToReg));

  // Notes on the sheet:
  //   Opcode
  //   rs1
  //   rs2
  //   rd
  //   rs2
  //   Imm
endmodule
